// Logisim project Practica 2. Tema 5. Jesús Rodríguez Heras.circ as structural Verilog: 1 circuit, main circuit main
module main (
  input  [15:0] in_1,
  input  in_2,
  input  [15:0] in_3,
  input  in_4,
  input  in_5,
  input  in_6,
  output [15:0] out_7
);

  wire decoder_1_out0, decoder_1_out1, decoder_1_out2;

  Decoder #(.select(2), .enable("false")) decoder_1 (
    .out0(decoder_1_out0), .out1(decoder_1_out1), .out2(decoder_1_out2), .sel(in_3[15:14]));  // open: out3
  assign out_7 = in_2 ? in_1 : 16'bz;  // Controlled_Buffer controlled_buffer_1
  RAM #(.addrWidth(14), .dataWidth(4)) ram_1 (
    .addr(in_3[13:0]), .data(out_7[3:0]), .sel(decoder_1_out0), .clk(in_4), .ld(in_5), .clr(in_6));
  RAM #(.addrWidth(14), .dataWidth(4)) ram_2 (
    .addr(in_3[13:0]), .data(out_7[3:0]), .sel(decoder_1_out1), .clk(in_4), .ld(in_5), .clr(in_6));
  RAM #(.addrWidth(14), .dataWidth(4)) ram_3 (
    .addr(in_3[13:0]), .data(out_7[3:0]), .sel(decoder_1_out2), .clk(in_4), .ld(in_5), .clr(in_6));
  RAM #(.addrWidth(14), .dataWidth(4)) ram_4 (
    .addr(in_3[13:0]), .data(out_7[7:4]), .sel(decoder_1_out0), .clk(in_4), .ld(in_5), .clr(in_6));
  RAM #(.addrWidth(14), .dataWidth(4)) ram_5 (
    .addr(in_3[13:0]), .data(out_7[7:4]), .sel(decoder_1_out1), .clk(in_4), .ld(in_5), .clr(in_6));
  RAM #(.addrWidth(14), .dataWidth(4)) ram_6 (
    .addr(in_3[13:0]), .data(out_7[7:4]), .sel(decoder_1_out2), .clk(in_4), .ld(in_5), .clr(in_6));
  RAM #(.addrWidth(14), .dataWidth(4)) ram_7 (
    .addr(in_3[13:0]), .data(out_7[11:8]), .sel(decoder_1_out0), .clk(in_4), .ld(in_5), .clr(in_6));
  RAM #(.addrWidth(14), .dataWidth(4)) ram_8 (
    .addr(in_3[13:0]), .data(out_7[11:8]), .sel(decoder_1_out1), .clk(in_4), .ld(in_5), .clr(in_6));
  RAM #(.addrWidth(14), .dataWidth(4)) ram_9 (
    .addr(in_3[13:0]), .data(out_7[11:8]), .sel(decoder_1_out2), .clk(in_4), .ld(in_5), .clr(in_6));
  RAM #(.addrWidth(14), .dataWidth(4)) ram_10 (
    .addr(in_3[13:0]), .data(out_7[15:12]), .sel(decoder_1_out0), .clk(in_4), .ld(in_5), .clr(in_6));
  RAM #(.addrWidth(14), .dataWidth(4)) ram_11 (
    .addr(in_3[13:0]), .data(out_7[15:12]), .sel(decoder_1_out1), .clk(in_4), .ld(in_5), .clr(in_6));
  RAM #(.addrWidth(14), .dataWidth(4)) ram_12 (
    .addr(in_3[13:0]), .data(out_7[15:12]), .sel(decoder_1_out2), .clk(in_4), .ld(in_5), .clr(in_6));
endmodule
