// Logisim project CPU_MIPS v3.5 (manual).circ as structural Verilog: 9 circuits, main circuit Main
module BANCO (
  input  [4:0] RA,
  input  [4:0] RB,
  input  [4:0] RC,
  input  [31:0] E,
  input  CS,
  output [31:0] A,
  output [31:0] B
);

  wire Reset;
  wire [3:0] demultiplexer_2_out0, demultiplexer_2_out4, demultiplexer_2_out8, demultiplexer_2_out12,
       demultiplexer_2_out16, demultiplexer_2_out20, demultiplexer_2_out24, demultiplexer_2_out31;
  wire [31:0] demultiplexer_1_out0, demultiplexer_1_out1, demultiplexer_1_out2, demultiplexer_1_out3,
       demultiplexer_1_out4, demultiplexer_1_out5, demultiplexer_1_out6, demultiplexer_1_out7,
       demultiplexer_1_out8, demultiplexer_1_out9, demultiplexer_1_out10, demultiplexer_1_out11,
       demultiplexer_1_out12, demultiplexer_1_out13, demultiplexer_1_out14, demultiplexer_1_out15,
       demultiplexer_1_out16, demultiplexer_1_out17, demultiplexer_1_out18, demultiplexer_1_out19,
       demultiplexer_1_out20, demultiplexer_1_out21, demultiplexer_1_out22, demultiplexer_1_out23,
       demultiplexer_1_out24, demultiplexer_1_out25, demultiplexer_1_out26, demultiplexer_1_out27,
       demultiplexer_1_out28, demultiplexer_1_out29, demultiplexer_1_out30, demultiplexer_1_out31,
       register_1_q, register_2_q, register_3_q, register_4_q, register_5_q, register_6_q, register_7_q,
       register_8_q, register_9_q, register_10_q, register_11_q, register_12_q, register_13_q, register_14_q,
       register_15_q, register_16_q, register_17_q, register_18_q, register_19_q, register_20_q,
       register_21_q, register_22_q, register_23_q, register_24_q, register_25_q, register_26_q,
       register_27_q, register_28_q, register_29_q, register_30_q, register_31_q, register_32_q;

  Register #(.width(32)) register_1 (
    .D(demultiplexer_1_out0), .Q(register_1_q), .clk(demultiplexer_2_out0[0]), .clr(Reset));  // open: en
  Register #(.width(32)) register_2 (
    .D(demultiplexer_1_out1), .Q(register_2_q), .clk(demultiplexer_2_out0[1]), .clr(Reset));  // open: en
  Register #(.width(32)) register_3 (
    .D(demultiplexer_1_out2), .Q(register_3_q), .clk(demultiplexer_2_out0[2]), .clr(Reset));  // open: en
  Register #(.width(32)) register_4 (
    .D(demultiplexer_1_out3), .Q(register_4_q), .clk(demultiplexer_2_out0[3]), .clr(Reset));  // open: en
  Demultiplexer #(.select(5), .width(32)) demultiplexer_1 (
    .out0(demultiplexer_1_out0), .out1(demultiplexer_1_out1), .out2(demultiplexer_1_out2),
    .out3(demultiplexer_1_out3), .out4(demultiplexer_1_out4), .out5(demultiplexer_1_out5),
    .out6(demultiplexer_1_out6), .out7(demultiplexer_1_out7), .out8(demultiplexer_1_out8),
    .out9(demultiplexer_1_out9), .out10(demultiplexer_1_out10), .out11(demultiplexer_1_out11),
    .out12(demultiplexer_1_out12), .out13(demultiplexer_1_out13), .out14(demultiplexer_1_out14),
    .out15(demultiplexer_1_out15), .out16(demultiplexer_1_out16), .out17(demultiplexer_1_out17),
    .out18(demultiplexer_1_out18), .out19(demultiplexer_1_out19), .out20(demultiplexer_1_out20),
    .out21(demultiplexer_1_out21), .out22(demultiplexer_1_out22), .out23(demultiplexer_1_out23),
    .out24(demultiplexer_1_out24), .out25(demultiplexer_1_out25), .out26(demultiplexer_1_out26),
    .out27(demultiplexer_1_out27), .out28(demultiplexer_1_out28), .out29(demultiplexer_1_out29),
    .out30(demultiplexer_1_out30), .out31(demultiplexer_1_out31), .in(E), .sel(RC));  // open: en
  Register #(.width(32)) register_5 (
    .D(demultiplexer_1_out4), .Q(register_5_q), .clk(demultiplexer_2_out4[0]), .clr(Reset));  // open: en
  Register #(.width(32)) register_6 (
    .D(demultiplexer_1_out5), .Q(register_6_q), .clk(demultiplexer_2_out4[1]), .clr(Reset));  // open: en
  Register #(.width(32)) register_7 (
    .D(demultiplexer_1_out6), .Q(register_7_q), .clk(demultiplexer_2_out4[2]), .clr(Reset));  // open: en
  Register #(.width(32)) register_8 (
    .D(demultiplexer_1_out7), .Q(register_8_q), .clk(demultiplexer_2_out4[3]), .clr(Reset));  // open: en
  Register #(.width(32)) register_9 (
    .D(demultiplexer_1_out8), .Q(register_9_q), .clk(demultiplexer_2_out8[0]), .clr(Reset));  // open: en
  Register #(.width(32)) register_10 (
    .D(demultiplexer_1_out9), .Q(register_10_q), .clk(demultiplexer_2_out8[1]), .clr(Reset));  // open: en
  Register #(.width(32)) register_11 (
    .D(demultiplexer_1_out10), .Q(register_11_q), .clk(demultiplexer_2_out8[2]), .clr(Reset));  // open: en
  Register #(.width(32)) register_12 (
    .D(demultiplexer_1_out11), .Q(register_12_q), .clk(demultiplexer_2_out8[3]), .clr(Reset));  // open: en
  Register #(.width(32)) register_13 (
    .D(demultiplexer_1_out12), .Q(register_13_q), .clk(demultiplexer_2_out12[0]), .clr(Reset));  // open: en
  Register #(.width(32)) register_14 (
    .D(demultiplexer_1_out13), .Q(register_14_q), .clk(demultiplexer_2_out12[1]), .clr(Reset));  // open: en
  Register #(.width(32)) register_15 (
    .D(demultiplexer_1_out14), .Q(register_15_q), .clk(demultiplexer_2_out12[2]), .clr(Reset));  // open: en
  Register #(.width(32)) register_16 (
    .D(demultiplexer_1_out15), .Q(register_16_q), .clk(demultiplexer_2_out12[3]), .clr(Reset));  // open: en
  Register #(.width(32)) register_17 (
    .D(demultiplexer_1_out16), .Q(register_17_q), .clk(demultiplexer_2_out16[0]), .clr(Reset));  // open: en
  Register #(.width(32)) register_18 (
    .D(demultiplexer_1_out17), .Q(register_18_q), .clk(demultiplexer_2_out16[1]), .clr(Reset));  // open: en
  Register #(.width(32)) register_19 (
    .D(demultiplexer_1_out18), .Q(register_19_q), .clk(demultiplexer_2_out16[2]), .clr(Reset));  // open: en
  Register #(.width(32)) register_20 (
    .D(demultiplexer_1_out19), .Q(register_20_q), .clk(demultiplexer_2_out16[3]), .clr(Reset));  // open: en
  Register #(.width(32)) register_21 (
    .D(demultiplexer_1_out20), .Q(register_21_q), .clk(demultiplexer_2_out20[0]), .clr(Reset));  // open: en
  Register #(.width(32)) register_22 (
    .D(demultiplexer_1_out21), .Q(register_22_q), .clk(demultiplexer_2_out20[1]), .clr(Reset));  // open: en
  Register #(.width(32)) register_23 (
    .D(demultiplexer_1_out22), .Q(register_23_q), .clk(demultiplexer_2_out20[2]), .clr(Reset));  // open: en
  Register #(.width(32)) register_24 (
    .D(demultiplexer_1_out23), .Q(register_24_q), .clk(demultiplexer_2_out20[3]), .clr(Reset));  // open: en
  Register #(.width(32)) register_25 (
    .D(demultiplexer_1_out24), .Q(register_25_q), .clk(demultiplexer_2_out24[0]), .clr(Reset));  // open: en
  Register #(.width(32)) register_26 (
    .D(demultiplexer_1_out25), .Q(register_26_q), .clk(demultiplexer_2_out24[1]), .clr(Reset));  // open: en
  Register #(.width(32)) register_27 (
    .D(demultiplexer_1_out26), .Q(register_27_q), .clk(demultiplexer_2_out24[2]), .clr(Reset));  // open: en
  Register #(.width(32)) register_28 (
    .D(demultiplexer_1_out27), .Q(register_28_q), .clk(demultiplexer_2_out24[3]), .clr(Reset));  // open: en
  Register #(.width(32)) register_29 (
    .D(demultiplexer_1_out28), .Q(register_29_q), .clk(demultiplexer_2_out31[0]), .clr(Reset));  // open: en
  Register #(.width(32)) register_30 (
    .D(demultiplexer_1_out29), .Q(register_30_q), .clk(demultiplexer_2_out31[1]), .clr(Reset));  // open: en
  Register #(.width(32)) register_31 (
    .D(demultiplexer_1_out30), .Q(register_31_q), .clk(demultiplexer_2_out31[2]), .clr(Reset));  // open: en
  Register #(.width(32)) register_32 (
    .D(demultiplexer_1_out31), .Q(register_32_q), .clk(demultiplexer_2_out31[3]), .clr(Reset));  // open: en
  Demultiplexer #(.select(5)) demultiplexer_2 (
    .out0(demultiplexer_2_out0[0]), .out1(demultiplexer_2_out0[1]), .out2(demultiplexer_2_out0[2]),
    .out3(demultiplexer_2_out0[3]), .out4(demultiplexer_2_out4[0]), .out5(demultiplexer_2_out4[1]),
    .out6(demultiplexer_2_out4[2]), .out7(demultiplexer_2_out4[3]), .out8(demultiplexer_2_out8[0]),
    .out9(demultiplexer_2_out8[1]), .out10(demultiplexer_2_out8[2]), .out11(demultiplexer_2_out8[3]),
    .out12(demultiplexer_2_out12[0]), .out13(demultiplexer_2_out12[1]), .out14(demultiplexer_2_out12[2]),
    .out15(demultiplexer_2_out12[3]), .out16(demultiplexer_2_out16[0]), .out17(demultiplexer_2_out16[1]),
    .out18(demultiplexer_2_out16[2]), .out19(demultiplexer_2_out16[3]), .out20(demultiplexer_2_out20[0]),
    .out21(demultiplexer_2_out20[1]), .out22(demultiplexer_2_out20[2]), .out23(demultiplexer_2_out20[3]),
    .out24(demultiplexer_2_out24[0]), .out25(demultiplexer_2_out24[1]), .out26(demultiplexer_2_out24[2]),
    .out27(demultiplexer_2_out24[3]), .out28(demultiplexer_2_out31[3]), .out29(demultiplexer_2_out31[1]),
    .out30(demultiplexer_2_out31[2]), .out31(demultiplexer_2_out31[0]), .in(CS), .sel(RC));  // open: en
  Multiplexer #(.select(5), .width(32)) multiplexer_1 (
    .in0(register_1_q), .in1(register_2_q), .in2(register_3_q), .in3(register_4_q), .in4(register_5_q),
    .in5(register_6_q), .in6(register_7_q), .in7(register_8_q), .in8(register_9_q), .in9(register_10_q),
    .in10(register_11_q), .in11(register_12_q), .in12(register_13_q), .in13(register_14_q),
    .in14(register_15_q), .in15(register_16_q), .in16(register_17_q), .in17(register_18_q),
    .in18(register_19_q), .in19(register_20_q), .in20(register_21_q), .in21(register_22_q),
    .in22(register_23_q), .in23(register_24_q), .in24(register_25_q), .in25(register_26_q),
    .in26(register_27_q), .in27(register_28_q), .in28(register_29_q), .in29(register_30_q),
    .in30(register_31_q), .in31(register_32_q), .out(A), .sel(RA));  // open: en
  Multiplexer #(.select(5), .width(32)) multiplexer_2 (
    .in0(register_1_q), .in1(register_2_q), .in2(register_3_q), .in3(register_4_q), .in4(register_5_q),
    .in5(register_6_q), .in6(register_7_q), .in7(register_8_q), .in8(register_9_q), .in9(register_10_q),
    .in10(register_11_q), .in11(register_12_q), .in12(register_13_q), .in13(register_14_q),
    .in14(register_15_q), .in15(register_16_q), .in16(register_17_q), .in17(register_18_q),
    .in18(register_19_q), .in19(register_20_q), .in20(register_21_q), .in21(register_22_q),
    .in22(register_23_q), .in23(register_24_q), .in24(register_25_q), .in25(register_26_q),
    .in26(register_27_q), .in27(register_28_q), .in28(register_29_q), .in29(register_30_q),
    .in30(register_31_q), .in31(register_32_q), .out(B), .sel(RB));  // open: en
endmodule

// MAIN
module Main (
  input  in_1,
  input  E,
  input  L,
  input  TA,
  input  TD,
  input  C2,
  input  C4,
  input  C6,
  input  C3,
  input  C5,
  input  T3,
  input  T4,
  input  T8,
  input  T9,
  input  C1,
  input  T7,
  input  T1,
  input  T2,
  input  T5,
  input  T6,
  input  C9,
  input  C10,
  input  C7,
  input  C8,
  input  MA,
  input  MB,
  input  [5:0] C__Op,
  input  [4:0] RA,
  input  [4:0] RB,
  input  RESET,
  input  [4:0] RC,
  input  SC,
  input  C11,
  output [31:0] BUS_DE_DATOS,
  output [31:0] BUS_INTERNO,
  output [31:0] INDICADORES,
  output [31:0] SALIDA_ALU
);

  wire not_1_out, not_2_out, not_3_out, or_1_out, or_2_out, or_3_out, xor_1_out, xor_2_out, xor_3_out;
  wire [1:0] controlled_buffer_1_out_2, controlled_buffer_1_out_3, controlled_buffer_1_out_4,
       controlled_buffer_1_out_5;
  wire [27:2] RI_q_2;
  wire [29:0] controlled_buffer_1_out;
  wire [31:0] adder_1_out, banco_1_a, banco_1_b, bit_extender_1_out, IND_q, MAR_q, MBR_q, multiplexer_1_out,
       multiplexer_2_out, multiplexer_3_out, multiplexer_4_out, multiplexer_5_out, PC_q, RT1_q, RT2_q, RT3_q;
  wire [31:26] RI_q;

  assign {controlled_buffer_1_out_5, controlled_buffer_1_out[29:14], controlled_buffer_1_out_4, controlled_buffer_1_out_3, controlled_buffer_1_out_2, controlled_buffer_1_out[7:0]} = TD ? MAR_q : 32'bz;  // Controlled_Buffer controlled_buffer_1
  Register #(.width(32)) MAR (.D(BUS_INTERNO), .Q(MAR_q), .clk(C1), .clr(RESET));  // open: en
  assign BUS_INTERNO = T1 ? banco_1_a : 32'bz;  // Controlled_Buffer controlled_buffer_2
  BANCO banco_1 (.RA(RA), .RB(RB), .RC(RC), .E(BUS_INTERNO), .CS(SC), .A(banco_1_a), .B(banco_1_b));
  assign BUS_INTERNO = T2 ? banco_1_b : 32'bz;  // Controlled_Buffer controlled_buffer_3
  not not_1 (not_1_out, C2);
  Register #(.width(32)) RT1 (.D(BUS_INTERNO), .Q(RT1_q), .clk(C9), .clr(RESET));  // open: en
  Multiplexer #(.width(32)) multiplexer_1 (
    .in0(banco_1_a), .in1(RT1_q), .out(multiplexer_1_out), .sel(MA));  // open: en
  ALU alu_1 (.Op__A(multiplexer_1_out), .Op__B(multiplexer_3_out), .C_OP(C__Op), .Estado(INDICADORES), .S(SALIDA_ALU));
  RAM #(.addrWidth(24), .dataWidth(32)) ram_1 (
    .addr({controlled_buffer_1_out[25:14], controlled_buffer_1_out_4, controlled_buffer_1_out_3, controlled_buffer_1_out_2, controlled_buffer_1_out[7:2]}),
    .data(BUS_DE_DATOS), .sel(in_1), .clk(E), .ld(L), .clr(RESET));
  Multiplexer #(.width(32)) multiplexer_2 (
    .in0(BUS_DE_DATOS), .in1(BUS_INTERNO), .out(multiplexer_2_out), .sel(or_1_out));  // open: en
  or or_1 (or_1_out, not_1_out, C3);
  xor xor_1 (xor_1_out, C2, C3);
  assign BUS_DE_DATOS = TA ? MBR_q : 32'bz;  // Controlled_Buffer controlled_buffer_4
  Register #(.width(32), .trigger("falling")) MBR (
    .D(multiplexer_2_out), .Q(MBR_q), .clk(xor_1_out), .clr(RESET));  // open: en
  assign BUS_INTERNO = T3 ? MBR_q : 32'bz;  // Controlled_Buffer controlled_buffer_5
  assign BUS_INTERNO = T5 ? SALIDA_ALU : 32'bz;  // Controlled_Buffer controlled_buffer_6
  Register #(.width(32)) RT2 (.D(BUS_INTERNO), .Q(RT2_q), .clk(C10), .clr(RESET));  // open: en
  Multiplexer #(.width(32)) multiplexer_3 (
    .in0(banco_1_b), .in1(RT2_q), .out(multiplexer_3_out), .sel(MB));  // open: en
  not not_2 (not_2_out, C4);
  assign BUS_INTERNO = T6 ? RT3_q : 32'bz;  // Controlled_Buffer controlled_buffer_7
  Register #(.width(32)) RT3 (.D(SALIDA_ALU), .Q(RT3_q), .clk(C11));  // open: en, clr
  Adder #(.width(32)) adder_1 (.a(PC_q), .b(32'h4), .out(adder_1_out));  // open: cin, cout
  or or_2 (or_2_out, not_2_out, C5);
  xor xor_2 (xor_2_out, C4, C5);
  Multiplexer #(.width(32)) multiplexer_4 (
    .in0(adder_1_out), .in1(BUS_INTERNO), .out(multiplexer_4_out), .sel(or_2_out));  // open: en
  Register #(.width(32), .trigger("falling")) PC (
    .D(multiplexer_4_out), .Q(PC_q), .clk(xor_2_out), .clr(RESET));  // open: en
  assign BUS_INTERNO = T4 ? PC_q : 32'bz;  // Controlled_Buffer controlled_buffer_8
  not not_3 (not_3_out, C7);
  Multiplexer #(.width(32)) multiplexer_5 (
    .in0(BUS_INTERNO), .in1(INDICADORES), .out(multiplexer_5_out), .sel(or_3_out));  // open: en
  or or_3 (or_3_out, not_3_out, C8);
  xor xor_3 (xor_3_out, C7, C8);
  Register #(.width(32)) RI (.D(BUS_INTERNO), .Q({RI_q, RI_q_2}), .clk(C6), .clr(RESET));  // open: en
  assign BUS_INTERNO = T7 ? IND_q : 32'bz;  // Controlled_Buffer controlled_buffer_9
  Register #(.width(32), .trigger("falling")) IND (
    .D(multiplexer_5_out), .Q(IND_q), .clk(xor_3_out), .clr(RESET));  // open: en
  assign bit_extender_1_out = {{16{RI_q_2[17]}}, RI_q_2[17:2]};  // Bit_Extender bit_extender_1
  assign BUS_INTERNO = T8 ? bit_extender_1_out : 32'bz;  // Controlled_Buffer controlled_buffer_10
  assign BUS_INTERNO = T9 ? {4'b0000, RI_q_2, 2'b00} : 32'bz;  // Controlled_Buffer controlled_buffer_11

  // Notes on the sheet:
  //   TD: pull=up
  //   Inmediato
  //   Jump Address
endmodule

module ALU (
  input  [31:0] Op__A,
  input  [31:0] Op__B,
  input  [5:0] C_OP,
  output [31:0] Estado,
  output [31:0] S
);

  wire Sel_aritlog_sel_al, Sel_Shift_sel_sh;
  wire [31:0] and_1_out, nor_1_out, or_1_out, S_R_s, SLL_s, SRA_s, xor_1_out;

  Sel_AritLog Sel_aritlog (.ALU_Func(C_OP[5:3]), .Sel_AL(Sel_aritlog_sel_al));
  assign and_1_out = Op__B & Op__A;  // AND_Gate and_1, 32 bits wide
  ALU_SUMA_RESTA S_R (.A(Op__A), .B(Op__B), .S_R(C_OP[0]), .S(S_R_s), .Carry(Estado[2]));
  Multiplexer #(.select(3), .width(32)) multiplexer_1 (
    .in0(S_R_s), .in1(S_R_s), .in2(S_R_s), .in3(S_R_s), .in4(and_1_out), .in5(or_1_out), .in6(xor_1_out),
    .in7(nor_1_out), .out(S), .sel(C_OP[2:0]), .en(Sel_aritlog_sel_al));
  assign xor_1_out = Op__B ^ Op__A;  // XOR_Gate xor_1, 32 bits wide
  assign or_1_out = Op__B | Op__A;  // OR_Gate or_1, 32 bits wide
  assign nor_1_out = ~(Op__B | Op__A);  // NOR_Gate nor_1, 32 bits wide
  ALU_Des_Izq SLL (.A(Op__A), .B(Op__B), .S(SLL_s));
  Multiplexer #(.select(3), .width(32)) multiplexer_2 (
    .in0(SLL_s), .in3(SRA_s), .out(S), .sel(C_OP[2:0]), .en(Sel_Shift_sel_sh));  // open: in1, in2, in4, in5, in6, in7
  Sel_Shift Sel_Shift (.ALU_Func(C_OP[5:3]), .Sel_Sh(Sel_Shift_sel_sh));
  ALU_Des_Der SRA (.A(Op__A), .B(Op__B), .S(SRA_s));
  nor nor_2 (Estado[0], S[0], S[1], S[2], S[3], S[4], S[5], S[6], S[7], S[8], S[9], S[10], S[11], S[12], S[13], S[14], S[15], S[16], S[17], S[18], S[19], S[20], S[21], S[22], S[23], S[24], S[25], S[26], S[27], S[28], S[29], S[30], S[31]);
  ExactlyOne xor_2 (
    .out(Estado[1]), .in0(S[0]), .in1(S[1]), .in2(S[2]), .in3(S[3]), .in4(S[4]), .in5(S[5]), .in6(S[6]),
    .in7(S[7]), .in8(S[8]), .in9(S[9]), .in10(S[10]), .in11(S[11]), .in12(S[12]), .in13(S[13]), .in14(S[14]),
    .in15(S[15]), .in16(S[16]), .in17(S[17]), .in18(S[18]), .in19(S[19]), .in20(S[20]), .in21(S[21]),
    .in22(S[22]), .in23(S[23]), .in24(S[24]), .in25(S[25]), .in26(S[26]), .in27(S[27]), .in28(S[28]),
    .in29(S[29]), .in30(S[30]), .in31(S[31]));

  assign Estado[31:3] = {29{1'b0}};

  // Other names for the same wires on the sheet: C = Estado[2]

  // Notes on the sheet:
  //   Estado: pull=down
endmodule

module ALU_SUMA_RESTA (
  input  [31:0] A,
  input  [31:0] B,
  input  S_R,
  output [31:0] S,
  output Carry
);

  wire [31:0] xor_1_out;

  assign xor_1_out = B ^ {32{S_R}};  // XOR_Gate xor_1, 32 bits wide
  Adder #(.width(32)) adder_1 (.a(A), .b(xor_1_out), .out(S), .cin(S_R), .cout(Carry));
endmodule

module ALU_Des_Izq (
  input  [31:0] A,
  input  [31:0] B,
  output [31:0] S
);

  wire [31:0] multiplexer_1_out, multiplexer_2_out, multiplexer_3_out, multiplexer_4_out;

  Multiplexer #(.width(32)) multiplexer_1 (
    .in0(A), .in1({A[30:0], 1'b0}), .out(multiplexer_1_out), .sel(B[0]));  // open: en
  Multiplexer #(.width(32)) multiplexer_2 (
    .in0(multiplexer_1_out), .in1({multiplexer_1_out[29:0], 2'b00}), .out(multiplexer_2_out), .sel(B[1]));  // open: en
  Multiplexer #(.width(32)) multiplexer_3 (
    .in0(multiplexer_2_out), .in1({multiplexer_2_out[27:0], 4'b0000}), .out(multiplexer_3_out), .sel(B[2]));  // open: en
  Multiplexer #(.width(32)) multiplexer_4 (
    .in0(multiplexer_3_out), .in1({multiplexer_3_out[23:0], {8{1'b0}}}), .out(multiplexer_4_out), .sel(B[3]));  // open: en
  Multiplexer #(.width(32)) multiplexer_5 (
    .in0(multiplexer_4_out), .in1({multiplexer_4_out[15:0], {16{1'b0}}}), .out(S), .sel(B[4]));  // open: en
endmodule

module ALU_Des_Der (
  input  [31:0] A,
  input  [31:0] B,
  output [31:0] S
);

  wire [31:0] multiplexer_1_out, multiplexer_2_out, multiplexer_3_out, multiplexer_4_out;

  Multiplexer #(.width(32)) multiplexer_1 (
    .in0(A), .in1({{2{A[31]}}, A[30:1]}), .out(multiplexer_1_out), .sel(B[0]));  // open: en
  Multiplexer #(.width(32)) multiplexer_2 (
    .in0(multiplexer_1_out), .in1({{3{multiplexer_1_out[31]}}, multiplexer_1_out[30:2]}),
    .out(multiplexer_2_out), .sel(B[1]));  // open: en
  Multiplexer #(.width(32)) multiplexer_3 (
    .in0(multiplexer_2_out), .in1({{4{multiplexer_2_out[31]}}, multiplexer_2_out[30:3]}),
    .out(multiplexer_3_out), .sel(B[2]));  // open: en
  Multiplexer #(.width(32)) multiplexer_4 (
    .in0(multiplexer_3_out), .in1({{8{multiplexer_3_out[31]}}, multiplexer_3_out[30:7]}),
    .out(multiplexer_4_out), .sel(B[3]));  // open: en
  Multiplexer #(.width(32)) multiplexer_5 (
    .in0(multiplexer_4_out), .in1({{16{multiplexer_4_out[31]}}, multiplexer_4_out[30:15]}), .out(S),
    .sel(B[4]));  // open: en
endmodule

module CONTROL (
  input  [31:0] RI,
  input  [31:0] EST,
  output T1,
  output T2,
  output T3,
  output MA,
  output T4,
  output MB,
  output T5,
  output SC,
  output T6,
  output C1,
  output T7,
  output C2,
  output T8,
  output C3,
  output T9,
  output C4,
  output Sin_uso,
  output C5,
  output TA,
  output C6,
  output TD,
  output C7,
  output MEM_L,
  output C8,
  output MEM_E,
  output C9,
  output MEM_Sel,
  output C10,
  output T1_2,
  output Sin_uso_2
);

  wire EXEC, NEXT;
  wire [7:0] adder_1_out, multiplexer_1_out, rom_1_data, RuI_q;

  ROM #(.addrWidth(6)) rom_1 (.addr(RI[31:26]), .data(rom_1_data));  // open: sel
  Adder adder_1 (.a(RuI_q), .b(8'h1), .out(adder_1_out));  // open: cin, cout
  Multiplexer #(.select(2), .width(8), .disabled(0), .enable("false")) multiplexer_1 (
    .in0({8{1'b0}}), .in1(adder_1_out), .in2(rom_1_data), .out(multiplexer_1_out), .sel({EXEC, NEXT}));  // open: in3
  Register RuI (.D(multiplexer_1_out), .Q(RuI_q));  // open: en, clk, clr
  ROM #(.dataWidth(32)) rom_2 (
    .addr(RuI_q),
    .data({T1_2, MEM_Sel, MEM_E, MEM_L, TD, TA, Sin_uso, T9, T8, T7, T6, T5, T4, T3, T2, T1, Sin_uso_2, C10, C9, C8, C7, C6, C5, C4, C3, C2, C1, SC, MB, MA, EXEC, NEXT}));  // open: sel

  // Notes on the sheet:
  //   T8: pull=down
  //   C2: pull=down
  //   C6: pull=down
  //   C9: pull=down
  //   C7: pull=down
  //   C4: pull=down
  //   T9: pull=down
  //   TA: pull=down
  //   SC: pull=down
  //   C3: pull=down
  //   MA: pull=down
  //   MEM_Sel: pull=down
  //   C1: pull=down
  //   C5: pull=down
  //   C8: pull=down
  //   TD: pull=down
  //   Sin_uso_2: pull=down
  //   T6: pull=down
  //   T4: pull=down
  //   C10: pull=down
  //   MB: pull=down
  //   T2: pull=down
  //   T1: pull=down
  //   T7: pull=down
  //   T1_2: pull=down
  //   MEM_L: pull=down
  //   T5: pull=down
  //   Sin_uso: pull=down
  //   MEM_E: pull=down
  //   T3: pull=down
  //   OPCODE
  //   Tabla direcciones
  //   Bits 19-16: Triestados
  //   Bits 23-20: Triestados
  //   Bits 27-24: Triestados
  //   Bits 31-28: Control Memoria
  //   00: Reset (vuelve a FETCH)
  //   10 = Exec: salta a la uInstr indicada por la tabla de direcciones
  //   11: No usado
  //   Bits 7-4: Señales captura
  //   Bits15-12: Señales de captura
  //   01 = Next: pasa a siguiente u-Instr en el siguiente ciclo
  //   Bits 3-0: MUX A y B; Control interno de la UC
  //   Bits 11-8: Señales captura
  //   Memoria de Microinstrucciones
  //   NEXT: Pasar a siguiente microinstrucción en el siguiente ciclo
  //   EXEC: RI está cargado; tomar de tabla direcciones la dirección
  //   del microprograma correspondiente a la instr. a ejecutar
endmodule

module Sel_Shift (
  input  [2:0] ALU_Func,
  output Sel_Sh
);

  and and_1 (Sel_Sh, ~ALU_Func[0], ~ALU_Func[1], ~ALU_Func[2]);  // AND_Gate

  // Notes on the sheet:
  //   ALU_func == 000: Desplazamiento de bits
endmodule

module Sel_AritLog (
  input  [2:0] ALU_Func,
  output Sel_AL
);

  wire and_1_out, and_2_out;

  and and_1 (and_1_out, ~ALU_Func[0], ~ALU_Func[1], ALU_Func[2]);  // AND_Gate
  and and_2 (and_2_out, ALU_Func[0], ~ALU_Func[1], ~ALU_Func[2]);  // AND_Gate
  or or_1 (Sel_AL, and_1_out, and_2_out);

  // Notes on the sheet:
  //   ALU_func == 001: Suma, resta u op. lógica tipo I
  //   ALU_func == 100: Suma, resta u op. lógica tipo R
endmodule
