// Logisim project CPU_MIPS_unidad_control_v1.00.circ as structural Verilog: 10 circuits, main circuit Main
module BANCO (
  input  [4:0] RA,
  input  [4:0] RB,
  input  [4:0] RC,
  input  [31:0] E,
  input  CS,
  output [31:0] A,
  output [31:0] B
);

  wire Reset;
  wire [3:0] demultiplexer_2_out0, demultiplexer_2_out4, demultiplexer_2_out8, demultiplexer_2_out12,
       demultiplexer_2_out16, demultiplexer_2_out20, demultiplexer_2_out24, demultiplexer_2_out31;
  wire [31:0] demultiplexer_1_out0, demultiplexer_1_out1, demultiplexer_1_out2, demultiplexer_1_out3,
       demultiplexer_1_out4, demultiplexer_1_out5, demultiplexer_1_out6, demultiplexer_1_out7,
       demultiplexer_1_out8, demultiplexer_1_out9, demultiplexer_1_out10, demultiplexer_1_out11,
       demultiplexer_1_out12, demultiplexer_1_out13, demultiplexer_1_out14, demultiplexer_1_out15,
       demultiplexer_1_out16, demultiplexer_1_out17, demultiplexer_1_out18, demultiplexer_1_out19,
       demultiplexer_1_out20, demultiplexer_1_out21, demultiplexer_1_out22, demultiplexer_1_out23,
       demultiplexer_1_out24, demultiplexer_1_out25, demultiplexer_1_out26, demultiplexer_1_out27,
       demultiplexer_1_out28, demultiplexer_1_out29, demultiplexer_1_out30, demultiplexer_1_out31,
       register_1_q, register_2_q, register_3_q, register_4_q, register_5_q, register_6_q, register_7_q,
       register_8_q, register_9_q, register_10_q, register_11_q, register_12_q, register_13_q, register_14_q,
       register_15_q, register_16_q, register_17_q, register_18_q, register_19_q, register_20_q,
       register_21_q, register_22_q, register_23_q, register_24_q, register_25_q, register_26_q,
       register_27_q, register_28_q, register_29_q, register_30_q, register_31_q, register_32_q;

  Register #(.width(32), .trigger("falling")) register_1 (
    .D(demultiplexer_1_out0), .en(1'b0), .Q(register_1_q), .clk(demultiplexer_2_out0[0]), .clr(Reset));
  Register #(.width(32), .trigger("falling")) register_2 (
    .D(demultiplexer_1_out1), .Q(register_2_q), .clk(demultiplexer_2_out0[1]), .clr(Reset));  // open: en
  Register #(.width(32), .trigger("falling")) register_3 (
    .D(demultiplexer_1_out2), .Q(register_3_q), .clk(demultiplexer_2_out0[2]), .clr(Reset));  // open: en
  Register #(.width(32), .trigger("falling")) register_4 (
    .D(demultiplexer_1_out3), .Q(register_4_q), .clk(demultiplexer_2_out0[3]), .clr(Reset));  // open: en
  Demultiplexer #(.select(5), .width(32)) demultiplexer_1 (
    .out0(demultiplexer_1_out0), .out1(demultiplexer_1_out1), .out2(demultiplexer_1_out2),
    .out3(demultiplexer_1_out3), .out4(demultiplexer_1_out4), .out5(demultiplexer_1_out5),
    .out6(demultiplexer_1_out6), .out7(demultiplexer_1_out7), .out8(demultiplexer_1_out8),
    .out9(demultiplexer_1_out9), .out10(demultiplexer_1_out10), .out11(demultiplexer_1_out11),
    .out12(demultiplexer_1_out12), .out13(demultiplexer_1_out13), .out14(demultiplexer_1_out14),
    .out15(demultiplexer_1_out15), .out16(demultiplexer_1_out16), .out17(demultiplexer_1_out17),
    .out18(demultiplexer_1_out18), .out19(demultiplexer_1_out19), .out20(demultiplexer_1_out20),
    .out21(demultiplexer_1_out21), .out22(demultiplexer_1_out22), .out23(demultiplexer_1_out23),
    .out24(demultiplexer_1_out24), .out25(demultiplexer_1_out25), .out26(demultiplexer_1_out26),
    .out27(demultiplexer_1_out27), .out28(demultiplexer_1_out28), .out29(demultiplexer_1_out29),
    .out30(demultiplexer_1_out30), .out31(demultiplexer_1_out31), .in(E), .sel(RC));  // open: en
  Register #(.width(32), .trigger("falling")) register_5 (
    .D(demultiplexer_1_out4), .Q(register_5_q), .clk(demultiplexer_2_out4[0]), .clr(Reset));  // open: en
  Register #(.width(32), .trigger("falling")) register_6 (
    .D(demultiplexer_1_out5), .Q(register_6_q), .clk(demultiplexer_2_out4[1]), .clr(Reset));  // open: en
  Register #(.width(32), .trigger("falling")) register_7 (
    .D(demultiplexer_1_out6), .Q(register_7_q), .clk(demultiplexer_2_out4[2]), .clr(Reset));  // open: en
  Register #(.width(32), .trigger("falling")) register_8 (
    .D(demultiplexer_1_out7), .Q(register_8_q), .clk(demultiplexer_2_out4[3]), .clr(Reset));  // open: en
  Register #(.width(32), .trigger("falling")) register_9 (
    .D(demultiplexer_1_out8), .Q(register_9_q), .clk(demultiplexer_2_out8[0]), .clr(Reset));  // open: en
  Register #(.width(32), .trigger("falling")) register_10 (
    .D(demultiplexer_1_out9), .Q(register_10_q), .clk(demultiplexer_2_out8[1]), .clr(Reset));  // open: en
  Register #(.width(32), .trigger("falling")) register_11 (
    .D(demultiplexer_1_out10), .Q(register_11_q), .clk(demultiplexer_2_out8[2]), .clr(Reset));  // open: en
  Register #(.width(32), .trigger("falling")) register_12 (
    .D(demultiplexer_1_out11), .Q(register_12_q), .clk(demultiplexer_2_out8[3]), .clr(Reset));  // open: en
  Register #(.width(32), .trigger("falling")) register_13 (
    .D(demultiplexer_1_out12), .Q(register_13_q), .clk(demultiplexer_2_out12[0]), .clr(Reset));  // open: en
  Register #(.width(32), .trigger("falling")) register_14 (
    .D(demultiplexer_1_out13), .Q(register_14_q), .clk(demultiplexer_2_out12[1]), .clr(Reset));  // open: en
  Register #(.width(32), .trigger("falling")) register_15 (
    .D(demultiplexer_1_out14), .Q(register_15_q), .clk(demultiplexer_2_out12[2]), .clr(Reset));  // open: en
  Register #(.width(32), .trigger("falling")) register_16 (
    .D(demultiplexer_1_out15), .Q(register_16_q), .clk(demultiplexer_2_out12[3]), .clr(Reset));  // open: en
  Register #(.width(32), .trigger("falling")) register_17 (
    .D(demultiplexer_1_out16), .Q(register_17_q), .clk(demultiplexer_2_out16[0]), .clr(Reset));  // open: en
  Register #(.width(32), .trigger("falling")) register_18 (
    .D(demultiplexer_1_out17), .Q(register_18_q), .clk(demultiplexer_2_out16[1]), .clr(Reset));  // open: en
  Register #(.width(32), .trigger("falling")) register_19 (
    .D(demultiplexer_1_out18), .Q(register_19_q), .clk(demultiplexer_2_out16[2]), .clr(Reset));  // open: en
  Register #(.width(32), .trigger("falling")) register_20 (
    .D(demultiplexer_1_out19), .Q(register_20_q), .clk(demultiplexer_2_out16[3]), .clr(Reset));  // open: en
  Register #(.width(32), .trigger("falling")) register_21 (
    .D(demultiplexer_1_out20), .Q(register_21_q), .clk(demultiplexer_2_out20[0]), .clr(Reset));  // open: en
  Register #(.width(32), .trigger("falling")) register_22 (
    .D(demultiplexer_1_out21), .Q(register_22_q), .clk(demultiplexer_2_out20[1]), .clr(Reset));  // open: en
  Register #(.width(32), .trigger("falling")) register_23 (
    .D(demultiplexer_1_out22), .Q(register_23_q), .clk(demultiplexer_2_out20[2]), .clr(Reset));  // open: en
  Register #(.width(32), .trigger("falling")) register_24 (
    .D(demultiplexer_1_out23), .Q(register_24_q), .clk(demultiplexer_2_out20[3]), .clr(Reset));  // open: en
  Register #(.width(32), .trigger("falling")) register_25 (
    .D(demultiplexer_1_out24), .Q(register_25_q), .clk(demultiplexer_2_out24[0]), .clr(Reset));  // open: en
  Register #(.width(32), .trigger("falling")) register_26 (
    .D(demultiplexer_1_out25), .Q(register_26_q), .clk(demultiplexer_2_out24[1]), .clr(Reset));  // open: en
  Register #(.width(32), .trigger("falling")) register_27 (
    .D(demultiplexer_1_out26), .Q(register_27_q), .clk(demultiplexer_2_out24[2]), .clr(Reset));  // open: en
  Register #(.width(32), .trigger("falling")) register_28 (
    .D(demultiplexer_1_out27), .Q(register_28_q), .clk(demultiplexer_2_out24[3]), .clr(Reset));  // open: en
  Register #(.width(32), .trigger("falling")) register_29 (
    .D(demultiplexer_1_out28), .Q(register_29_q), .clk(demultiplexer_2_out31[0]), .clr(Reset));  // open: en
  Register #(.width(32), .trigger("falling")) register_30 (
    .D(demultiplexer_1_out29), .Q(register_30_q), .clk(demultiplexer_2_out31[1]), .clr(Reset));  // open: en
  Register #(.width(32), .trigger("falling")) register_31 (
    .D(demultiplexer_1_out30), .Q(register_31_q), .clk(demultiplexer_2_out31[2]), .clr(Reset));  // open: en
  Register #(.width(32), .trigger("falling")) register_32 (
    .D(demultiplexer_1_out31), .Q(register_32_q), .clk(demultiplexer_2_out31[3]), .clr(Reset));  // open: en
  Demultiplexer #(.select(5)) demultiplexer_2 (
    .out0(demultiplexer_2_out0[0]), .out1(demultiplexer_2_out0[1]), .out2(demultiplexer_2_out0[2]),
    .out3(demultiplexer_2_out0[3]), .out4(demultiplexer_2_out4[0]), .out5(demultiplexer_2_out4[1]),
    .out6(demultiplexer_2_out4[2]), .out7(demultiplexer_2_out4[3]), .out8(demultiplexer_2_out8[0]),
    .out9(demultiplexer_2_out8[1]), .out10(demultiplexer_2_out8[2]), .out11(demultiplexer_2_out8[3]),
    .out12(demultiplexer_2_out12[0]), .out13(demultiplexer_2_out12[1]), .out14(demultiplexer_2_out12[2]),
    .out15(demultiplexer_2_out12[3]), .out16(demultiplexer_2_out16[0]), .out17(demultiplexer_2_out16[1]),
    .out18(demultiplexer_2_out16[2]), .out19(demultiplexer_2_out16[3]), .out20(demultiplexer_2_out20[0]),
    .out21(demultiplexer_2_out20[1]), .out22(demultiplexer_2_out20[2]), .out23(demultiplexer_2_out20[3]),
    .out24(demultiplexer_2_out24[0]), .out25(demultiplexer_2_out24[1]), .out26(demultiplexer_2_out24[2]),
    .out27(demultiplexer_2_out24[3]), .out28(demultiplexer_2_out31[3]), .out29(demultiplexer_2_out31[1]),
    .out30(demultiplexer_2_out31[2]), .out31(demultiplexer_2_out31[0]), .in(CS), .sel(RC));  // open: en
  Multiplexer #(.select(5), .width(32)) multiplexer_1 (
    .in0(register_1_q), .in1(register_2_q), .in2(register_3_q), .in3(register_4_q), .in4(register_5_q),
    .in5(register_6_q), .in6(register_7_q), .in7(register_8_q), .in8(register_9_q), .in9(register_10_q),
    .in10(register_11_q), .in11(register_12_q), .in12(register_13_q), .in13(register_14_q),
    .in14(register_15_q), .in15(register_16_q), .in16(register_17_q), .in17(register_18_q),
    .in18(register_19_q), .in19(register_20_q), .in20(register_21_q), .in21(register_22_q),
    .in22(register_23_q), .in23(register_24_q), .in24(register_25_q), .in25(register_26_q),
    .in26(register_27_q), .in27(register_28_q), .in28(register_29_q), .in29(register_30_q),
    .in30(register_31_q), .in31(register_32_q), .out(A), .sel(RA));  // open: en
  Multiplexer #(.select(5), .width(32)) multiplexer_2 (
    .in0(register_1_q), .in1(register_2_q), .in2(register_3_q), .in3(register_4_q), .in4(register_5_q),
    .in5(register_6_q), .in6(register_7_q), .in7(register_8_q), .in8(register_9_q), .in9(register_10_q),
    .in10(register_11_q), .in11(register_12_q), .in12(register_13_q), .in13(register_14_q),
    .in14(register_15_q), .in15(register_16_q), .in16(register_17_q), .in17(register_18_q),
    .in18(register_19_q), .in19(register_20_q), .in20(register_21_q), .in21(register_22_q),
    .in22(register_23_q), .in23(register_24_q), .in24(register_25_q), .in25(register_26_q),
    .in26(register_27_q), .in27(register_28_q), .in28(register_29_q), .in29(register_30_q),
    .in30(register_31_q), .in31(register_32_q), .out(B), .sel(RB));  // open: en
endmodule

// MAIN
module Main (
  input  RESET,
  output [31:0] BUS_DE_DATOS,
  output [31:0] BUS_INTERNO,
  output [31:0] INDICADORES,
  output [31:0] SALIDA_ALU
);

  wire C1, C2, C3, C4, C5, C6, C7, C8, C9, C10, C11, clock_1_out, clock_2_out, clock_3_out, E, L, M_Sel, MA,
       MB, or_1_out, or_2_out, or_3_out, SC, T1, T2, T3, T4, T5, T6, T7, T8, T9, TA;
  wire [1:0] MAR_q, MAR_q_2, MAR_q_3, MAR_q_4, MAR_q_5, MAR_q_6, MAR_q_7, MAR_q_9;
  wire [4:0] RA, RB, RC;
  wire [5:0] func;
  wire [29:14] MAR_q_8;
  wire [31:0] adder_1_out, banco_1_a, banco_1_b, bit_extender_1_out, IND_q, MBR_q, multiplexer_1_out,
       multiplexer_2_out, multiplexer_3_out, multiplexer_4_out, multiplexer_5_out, PC_q, RI, RT1_q, RT2_q,
       RT3_q;

  Register #(.width(32), .trigger("falling")) MAR (
    .D(BUS_INTERNO), .Q({MAR_q_9, MAR_q_8, MAR_q_7, MAR_q_6, MAR_q_5, MAR_q_4, MAR_q_3, MAR_q_2, MAR_q}),
    .clk(C1), .clr(RESET));  // open: en
  assign BUS_INTERNO = T1 ? banco_1_a : 32'bz;  // Controlled_Buffer controlled_buffer_1
  BANCO banco_1 (.RA(RA), .RB(RB), .RC(RC), .E(BUS_INTERNO), .CS(SC), .A(banco_1_a), .B(banco_1_b));
  assign BUS_INTERNO = T2 ? banco_1_b : 32'bz;  // Controlled_Buffer controlled_buffer_2
  Register #(.width(32), .trigger("falling")) RT1 (.D(BUS_INTERNO), .Q(RT1_q), .clk(C9), .clr(RESET));  // open: en
  Multiplexer #(.width(32)) multiplexer_1 (
    .in0(banco_1_a), .in1(RT1_q), .out(multiplexer_1_out), .sel(MA));  // open: en
  ALU alu_1 (.Op__A(multiplexer_1_out), .Op__B(multiplexer_3_out), .C_OP(func), .Estado(INDICADORES), .S(SALIDA_ALU));
  RAM #(.addrWidth(24), .dataWidth(32)) ram_1 (
    .addr({MAR_q_8[25:14], MAR_q_7, MAR_q_6, MAR_q_5, MAR_q_4, MAR_q_3, MAR_q_2}), .data(BUS_DE_DATOS),
    .sel(E), .clk(M_Sel), .ld(L));  // open: clr
  Multiplexer #(.width(32)) multiplexer_2 (
    .in0(BUS_DE_DATOS), .in1(BUS_INTERNO), .out(multiplexer_2_out), .sel(C3));  // open: en
  or or_1 (or_1_out, C2, C3);
  assign BUS_DE_DATOS = TA ? MBR_q : 32'bz;  // Controlled_Buffer controlled_buffer_3
  Register #(.width(32), .trigger("falling")) MBR (
    .D(multiplexer_2_out), .en(or_1_out), .Q(MBR_q), .clk(clock_1_out), .clr(RESET));
  Clock clock_1 (.out(clock_1_out));
  assign BUS_INTERNO = T3 ? MBR_q : 32'bz;  // Controlled_Buffer controlled_buffer_4
  assign BUS_INTERNO = T5 ? SALIDA_ALU : 32'bz;  // Controlled_Buffer controlled_buffer_5
  Register #(.width(32), .trigger("falling")) RT2 (.D(BUS_INTERNO), .Q(RT2_q), .clk(C10), .clr(RESET));  // open: en
  Multiplexer #(.width(32)) multiplexer_3 (
    .in0(banco_1_b), .in1(RT2_q), .out(multiplexer_3_out), .sel(MB));  // open: en
  assign BUS_INTERNO = T6 ? RT3_q : 32'bz;  // Controlled_Buffer controlled_buffer_6
  Register #(.width(32), .trigger("falling")) RT3 (.D(SALIDA_ALU), .Q(RT3_q), .clk(C11));  // open: en, clr
  Adder #(.width(32)) adder_1 (.a(PC_q), .b(32'h4), .out(adder_1_out));  // open: cin, cout
  Multiplexer #(.width(32)) multiplexer_4 (
    .in0(adder_1_out), .in1(BUS_INTERNO), .out(multiplexer_4_out), .sel(C5));  // open: en
  Register #(.width(32), .trigger("falling")) PC (
    .D(multiplexer_4_out), .en(or_2_out), .Q(PC_q), .clk(clock_2_out), .clr(RESET));
  Clock clock_2 (.out(clock_2_out));
  or or_2 (or_2_out, C4, C5);
  assign BUS_INTERNO = T4 ? PC_q : 32'bz;  // Controlled_Buffer controlled_buffer_7
  Multiplexer #(.width(32)) multiplexer_5 (
    .in0(BUS_INTERNO), .in1(INDICADORES), .out(multiplexer_5_out), .sel(C8));  // open: en
  or or_3 (or_3_out, C7, C8);
  Register #(.width(32), .trigger("falling")) u_RI (.D(BUS_INTERNO), .Q(RI), .clk(C6), .clr(RESET));  // open: en
  assign BUS_INTERNO = T7 ? IND_q : 32'bz;  // Controlled_Buffer controlled_buffer_8
  Register #(.width(32), .trigger("falling")) IND (
    .D(multiplexer_5_out), .en(or_3_out), .Q(IND_q), .clk(clock_3_out), .clr(RESET));
  Clock clock_3 (.out(clock_3_out));
  assign bit_extender_1_out = {{16{RI[15]}}, RI[15:0]};  // Bit_Extender bit_extender_1
  assign BUS_INTERNO = T8 ? bit_extender_1_out : 32'bz;  // Controlled_Buffer controlled_buffer_9
  assign BUS_INTERNO = T9 ? {4'b0000, RI[25:0], 2'b00} : 32'bz;  // Controlled_Buffer controlled_buffer_10
  CONTROL control_1 (
    .RI(RI), .EST(IND_q), .T1(T1), .T2(T2), .T3(T3), .T4(T4), .T5(T5), .SC(SC), .T6(T6), .C1(C1), .T7(T7),
    .C2(C2), .T8(T8), .C3(C3), .T9(T9), .C4(C4), .C5(C5), .MB(MB), .C6(C6), .MA(MA), .C7(C7), .MEM_L(L),
    .C8(C8), .MEM_E(E), .C9(C9), .MEM_Sel(M_Sel), .C10(C10), .TA(TA), .Sin_uso_2(C11), .ALU_func(func),
    .RC(RC), .RB(RB), .RA(RA), .RESET(RESET));  // open: Sin_uso, shamt

  // Notes on the sheet:
  //   Inmediato
  //   Jump Address
  //   CONTROL
endmodule

module ALU (
  input  [31:0] Op__A,
  input  [31:0] Op__B,
  input  [5:0] C_OP,
  output [31:0] Estado,
  output [31:0] S
);

  wire Sel_aritlog_sel_al, Sel_Shift_sel_sh;
  wire [31:0] and_1_out, nor_1_out, or_1_out, S_R_s, SLL_s, SRA_s, xor_1_out;

  Sel_AritLog Sel_aritlog (.ALU_Func(C_OP[5:3]), .Sel_AL(Sel_aritlog_sel_al));
  assign and_1_out = Op__B & Op__A;  // AND_Gate and_1, 32 bits wide
  ALU_SUMA_RESTA S_R (.A(Op__A), .B(Op__B), .S_R(C_OP[1]), .S(S_R_s), .Carry(Estado[2]));
  Multiplexer #(.select(3), .width(32)) multiplexer_1 (
    .in0(S_R_s), .in1(S_R_s), .in2(S_R_s), .in3(S_R_s), .in4(and_1_out), .in5(or_1_out), .in6(xor_1_out),
    .in7(nor_1_out), .out(S), .sel(C_OP[2:0]), .en(Sel_aritlog_sel_al));
  assign xor_1_out = Op__B ^ Op__A;  // XOR_Gate xor_1, 32 bits wide
  assign or_1_out = Op__B | Op__A;  // OR_Gate or_1, 32 bits wide
  assign nor_1_out = ~(Op__B | Op__A);  // NOR_Gate nor_1, 32 bits wide
  ALU_Des_Izq SLL (.A(Op__A), .B(Op__B), .S(SLL_s));
  Multiplexer #(.select(3), .width(32)) multiplexer_2 (
    .in0(SLL_s), .in3(SRA_s), .out(S), .sel(C_OP[2:0]), .en(Sel_Shift_sel_sh));  // open: in1, in2, in4, in5, in6, in7
  Sel_Shift Sel_Shift (.ALU_Func(C_OP[5:3]), .Sel_Sh(Sel_Shift_sel_sh));
  ALU_Des_Der SRA (.A(Op__A), .B(Op__B), .S(SRA_s));
  nor nor_2 (Estado[0], S[0], S[1], S[2], S[3], S[4], S[5], S[6], S[7], S[8], S[9], S[10], S[11], S[12], S[13], S[14], S[15], S[16], S[17], S[18], S[19], S[20], S[21], S[22], S[23], S[24], S[25], S[26], S[27], S[28], S[29], S[30], S[31]);
  ExactlyOne xor_2 (
    .out(Estado[1]), .in0(S[0]), .in1(S[1]), .in2(S[2]), .in3(S[3]), .in4(S[4]), .in5(S[5]), .in6(S[6]),
    .in7(S[7]), .in8(S[8]), .in9(S[9]), .in10(S[10]), .in11(S[11]), .in12(S[12]), .in13(S[13]), .in14(S[14]),
    .in15(S[15]), .in16(S[16]), .in17(S[17]), .in18(S[18]), .in19(S[19]), .in20(S[20]), .in21(S[21]),
    .in22(S[22]), .in23(S[23]), .in24(S[24]), .in25(S[25]), .in26(S[26]), .in27(S[27]), .in28(S[28]),
    .in29(S[29]), .in30(S[30]), .in31(S[31]));

  assign Estado[31:3] = {29{1'b0}};

  // Other names for the same wires on the sheet: C = Estado[2]

  // Notes on the sheet:
  //   Estado: pull=down
endmodule

module ALU_SUMA_RESTA (
  input  [31:0] A,
  input  [31:0] B,
  input  S_R,
  output [31:0] S,
  output Carry
);

  wire [31:0] xor_1_out;

  assign xor_1_out = B ^ {32{S_R}};  // XOR_Gate xor_1, 32 bits wide
  Adder #(.width(32)) adder_1 (.a(A), .b(xor_1_out), .out(S), .cin(S_R), .cout(Carry));
endmodule

module ALU_Des_Izq (
  input  [31:0] A,
  input  [31:0] B,
  output [31:0] S
);

  Multiplexer #(.select(2), .width(32)) multiplexer_1 (
    .in0({A[30:0], 1'b0}), .in1({A[29:0], 2'b00}), .in2({A[28:0], 3'b000}), .in3({A[27:0], 4'b0000}),
    .out(S), .sel(B[1:0]));  // open: en
endmodule

module ALU_Des_Der (
  input  [31:0] A,
  input  [31:0] B,
  output [31:0] S
);

  Multiplexer #(.select(2), .width(32)) multiplexer_1 (
    .in0({1'b0, A[31:1]}), .in1({2'b00, A[31:2]}), .in2({3'b000, A[31:3]}), .in3({4'b0000, A[31:4]}),
    .out(S), .sel(B[1:0]));  // open: en
endmodule

module CONTROL (
  input  [31:0] RI,
  input  RESET,
  input  [31:0] EST,
  output T1,
  output T2,
  output T3,
  output T4,
  output T5,
  output SC,
  output T6,
  output C1,
  output T7,
  output C2,
  output T8,
  output C3,
  output T9,
  output C4,
  output Sin_uso,
  output C5,
  output MB,
  output C6,
  output MA,
  output C7,
  output MEM_L,
  output C8,
  output MEM_E,
  output C9,
  output MEM_Sel,
  output C10,
  output TA,
  output Sin_uso_2,
  output [5:0] ALU_func,
  output [4:0] shamt,
  output [4:0] RC,
  output [4:0] RB,
  output [4:0] RA
);

  wire clock_1_out, EXEC, NEXT, Type_I;
  wire [3:3] rom_2_data;
  wire [7:0] adder_1_out, multiplexer_2_out, rom_1_data, RuI_q;

  ROM #(.addrWidth(6)) rom_1 (.addr(RI[31:26]), .data(rom_1_data));  // open: sel
  Multiplexer #(.width(6)) multiplexer_1 (.in0(RI[5:0]), .in1(RI[31:26]), .out(ALU_func), .sel(Type_I));  // open: en
  Adder adder_1 (.a(RuI_q), .b(8'h1), .out(adder_1_out));  // open: cin, cout
  Multiplexer #(.select(2), .width(8), .disabled(0), .enable("false")) multiplexer_2 (
    .in0({8{1'b0}}), .in1(adder_1_out), .in2(rom_1_data), .out(multiplexer_2_out), .sel({EXEC, NEXT}));  // open: in3
  Multiplexer #(.width(5)) multiplexer_3 (.in0(RI[15:11]), .in1(RI[20:16]), .out(RC), .sel(Type_I));  // open: en
  Register #(.trigger("falling")) RuI (.D(multiplexer_2_out), .Q(RuI_q), .clk(clock_1_out), .clr(RESET));  // open: en
  Clock clock_1 (.out(clock_1_out));
  ROM #(.dataWidth(32)) rom_2 (
    .addr(RuI_q),
    .data({TA, MEM_Sel, MEM_E, MEM_L, MA, MB, Sin_uso, T9, T8, T7, T6, T5, T4, T3, T2, T1, Sin_uso_2, C10, C9, C8, C7, C6, C5, C4, C3, C2, C1, SC, rom_2_data[3], Type_I, EXEC, NEXT}));  // open: sel

  assign RA = RI[25:21];
  assign RB = RI[20:16];
  assign shamt = RI[10:6];

  // Notes on the sheet:
  //   C1: pull=down
  //   T9: pull=down
  //   C9: pull=down
  //   MEM_E: pull=down
  //   MEM_L: pull=down
  //   T1: pull=down
  //   T2: pull=down
  //   SC: pull=down
  //   C5: pull=down
  //   RESET: pull=down
  //   MB: pull=down
  //   MEM_Sel: pull=down
  //   MA: pull=down
  //   C10: pull=down
  //   RI: pull=down
  //   T4: pull=down
  //   T3: pull=down
  //   C4: pull=down
  //   C2: pull=down
  //   Sin_uso_2: pull=down
  //   C8: pull=down
  //   T7: pull=down
  //   C3: pull=down
  //   T6: pull=down
  //   Sin_uso: pull=down
  //   C7: pull=down
  //   TA: pull=down
  //   T5: pull=down
  //   C6: pull=down
  //   T8: pull=down
  //   OPCODE
  //   Tabla direcciones
  //   contents of rom_1 (hex, n*v repeats v):
  //   5 0 d 5*0 10 26*0 6 7*0 9
  //   Bits 19-16: Triestados
  //   Bits 23-20: Triestados
  //   Bits 27-24: Triestados y MUX
  //   Bits 31-28: Control Memoria
  //   00: Reset (vuelve a FETCH)
  //   10 = Exec: salta a la uInstr indicada por la tabla de direcciones
  //   11: No usado
  //   Bits 7-4: Señales captura
  //   Bits15-12: Señales de captura
  //   01 = Next: pasa a siguiente u-Instr en el siguiente ciclo
  //   Bits 3-0: MUX A y B; Control interno de la UC
  //   Bits 11-8: Señales captura
  //   Memoria de Microinstrucciones
  //   contents of rom_2 (hex, n*v repeats v):
  //   80021 30000141 2040401 2 0 100010 80025 30000145 40014 10085 80025 a0000005 e0000004 1000220 0 0
  //   30000045 40405 804005 4100014
  //   NEXT: Pasar a siguiente microinstrucción en el siguiente ciclo
  //   EXEC: RI está cargado; leer de tabla direcciones
  //   Type_I: La instrucción en ejecución es de tipo I (con dato inmediato)
endmodule

module Generador_uInstr (
  input  T1,
  input  Next,
  input  T2,
  input  EXEC,
  input  T3,
  input  Type_I,
  input  T4,
  input  T5,
  input  SC,
  input  T6,
  input  C1,
  input  T7,
  input  C2,
  input  T8,
  input  C3,
  input  T9,
  input  C4,
  input  Sin_uso,
  input  C5,
  input  MB,
  input  C6,
  input  MA,
  input  C7,
  input  MEM_L,
  input  C8,
  input  MEM_E,
  input  C9,
  input  MEM_Sel,
  input  C10,
  input  TA,
  input  Sin_uso_2
);

  Hex_Digit_Display hex_digit_display_1 (.value({TA, MEM_Sel, MEM_E, MEM_L}));  // open: dp
  Hex_Digit_Display hex_digit_display_2 (.value({MA, MB, Sin_uso, T9}));  // open: dp
  Hex_Digit_Display hex_digit_display_3 (.value({T8, T7, T6, T5}));  // open: dp
  Hex_Digit_Display hex_digit_display_4 (.value({T4, T3, T2, T1}));  // open: dp
  Hex_Digit_Display hex_digit_display_5 (.value({Sin_uso_2, C10, C9, C8}));  // open: dp
  Hex_Digit_Display hex_digit_display_6 (.value({C3, C2, C1, SC}));  // open: dp
  Hex_Digit_Display hex_digit_display_7 (.value({C7, C6, C5, C4}));  // open: dp
  Hex_Digit_Display hex_digit_display_8 (.value({1'b0, Type_I, EXEC, Next}));  // open: dp

  // Notes on the sheet:
  //   C6: pull=down
  //   C1: pull=down
  //   MB: pull=down
  //   C10: pull=down
  //   C9: pull=down
  //   T5: pull=down
  //   C2: pull=down
  //   MEM_Sel: pull=down
  //   SC: pull=down
  //   T6: pull=down
  //   T8: pull=down
  //   EXEC: pull=down
  //   C7: pull=down
  //   MEM_L: pull=down
  //   C4: pull=down
  //   T7: pull=down
  //   Type_I: pull=down
  //   T4: pull=down
  //   TA: pull=down
  //   MA: pull=down
  //   T9: pull=down
  //   MEM_E: pull=down
  //   Sin_uso_2: pull=down
  //   C8: pull=down
  //   C3: pull=down
  //   T2: pull=down
  //   C5: pull=down
  //   T3: pull=down
  //   Sin_uso: pull=down
  //   T1: pull=down
  //   Next: pull=down
  //   Bits 19-16: Triestados
  //   Bits 23-20: Triestados
  //   Bits 27-24: Triestados y MUX
  //   Bits 31-28: Control Memoria
  //   Bits 3-0: MUX A y B; Control interno de la UC
  //   Bits 7-4: Señales captura
  //   Bits 11-8: Señales captura
  //   Bits15-12: Señales de captura
endmodule

module Sel_AritLog (
  input  [2:0] ALU_Func,
  output Sel_AL
);

  wire and_1_out, and_2_out;

  and and_1 (and_1_out, ~ALU_Func[0], ~ALU_Func[1], ALU_Func[2]);  // AND_Gate
  and and_2 (and_2_out, ALU_Func[0], ~ALU_Func[1], ~ALU_Func[2]);  // AND_Gate
  or or_1 (Sel_AL, and_1_out, and_2_out);

  // Notes on the sheet:
  //   ALU_func == 001: Suma, resta u op. lógica tipo I
  //   ALU_func == 100: Suma, resta u op. lógica tipo R
endmodule

module Sel_Shift (
  input  [2:0] ALU_Func,
  output Sel_Sh
);

  and and_1 (Sel_Sh, ~ALU_Func[0], ~ALU_Func[1], ~ALU_Func[2]);  // AND_Gate

  // Notes on the sheet:
  //   ALU_func == 000: Desplazamiento de bits
endmodule
