// Logisim project DAAC PR1_2.circ as structural Verilog: 1 circuit, main circuit main
module main (
  input  in_1,
  input  in_2,
  input  in_3,
  input  in_4,
  input  in_5,
  input  in_6,
  input  in_7,
  input  in_8,
  input  in_9,
  input  in_10,
  input  in_11,
  input  in_12,
  input  in_13,
  input  in_14,
  input  in_15,
  input  in_16
);

  wire and_1_out, and_2_out, and_3_out, and_4_out, and_5_out, clock_1_out, demultiplexer_1_out0,
       demultiplexer_1_out1, demultiplexer_1_out2, demultiplexer_1_out3, nor_1_out, not_1_out, not_2_out,
       not_3_out, not_4_out, not_5_out, not_6_out, shift_register_1_out;
  wire [1:0] register_1_q;
  wire [3:0] counter_1_q;
  wire [7:0] register_2_q, register_3_q, register_4_q, register_5_q, shift_register_2_q7,
       shift_register_3_q7, shift_register_4_q7, shift_register_5_q7;

  Shift_Register shift_register_1 (
    .shift(in_9), .in(in_11), .clk(and_1_out), .out(shift_register_1_out), .load(in_12), .d0(in_1),
    .d1(in_2), .d2(in_2), .d3(in_2), .d4(in_3), .d5(in_4), .d6(in_5), .d7(in_6));  // open: clr, q0, q1, q2, q3, q4, q5, q6, q7
  Counter #(.width(4), .max('hf)) counter_1 (
    .Q(counter_1_q), .clk(not_1_out), .clr(in_12));  // open: load, D, count, carry
  not not_1 (not_1_out, and_1_out);
  not not_2 (not_2_out, counter_1_q[3]);
  Clock clock_1 (.out(clock_1_out));
  and and_1 (and_1_out, clock_1_out, not_2_out);
  Demultiplexer #(.select(2)) demultiplexer_1 (
    .out0(demultiplexer_1_out0), .out1(demultiplexer_1_out1), .out2(demultiplexer_1_out2),
    .out3(demultiplexer_1_out3), .in(shift_register_1_out), .sel(register_1_q), .en(in_14));
  Register #(.width(2)) register_1 (.D({in_2, in_1}), .en(nor_1_out), .Q(register_1_q), .clk(in_12));  // open: clr
  nor nor_1 (nor_1_out, counter_1_q[0], counter_1_q[1], counter_1_q[2], counter_1_q[3]);
  not not_3 (not_3_out, shift_register_2_q7[7]);
  and and_2 (and_2_out, not_3_out, not_4_out);
  Shift_Register shift_register_2 (
    .shift(in_10), .in(demultiplexer_1_out0), .clk(and_1_out), .q0(shift_register_2_q7[7]),
    .q1(shift_register_2_q7[6]), .q2(shift_register_2_q7[5]), .q3(shift_register_2_q7[4]),
    .q4(shift_register_2_q7[3]), .q5(shift_register_2_q7[2]), .q6(shift_register_2_q7[1]),
    .q7(shift_register_2_q7[0]));  // open: out, load, clr, d0, d1, d2, d3, d4, d5, d6, d7
  not not_4 (not_4_out, shift_register_2_q7[6]);
  Shift_Register shift_register_3 (
    .shift(in_13), .in(demultiplexer_1_out1), .clk(and_1_out), .q0(shift_register_3_q7[7]),
    .q1(shift_register_3_q7[6]), .q2(shift_register_3_q7[5]), .q3(shift_register_3_q7[4]),
    .q4(shift_register_3_q7[3]), .q5(shift_register_3_q7[2]), .q6(shift_register_3_q7[1]),
    .q7(shift_register_3_q7[0]));  // open: out, load, clr, d0, d1, d2, d3, d4, d5, d6, d7
  not not_5 (not_5_out, shift_register_3_q7[7]);
  and and_3 (and_3_out, not_5_out, shift_register_3_q7[6]);
  Shift_Register shift_register_4 (
    .shift(in_15), .in(demultiplexer_1_out2), .clk(and_1_out), .q0(shift_register_4_q7[7]),
    .q1(shift_register_4_q7[6]), .q2(shift_register_4_q7[5]), .q3(shift_register_4_q7[4]),
    .q4(shift_register_4_q7[3]), .q5(shift_register_4_q7[2]), .q6(shift_register_4_q7[1]),
    .q7(shift_register_4_q7[0]));  // open: out, load, clr, d0, d1, d2, d3, d4, d5, d6, d7
  not not_6 (not_6_out, shift_register_4_q7[6]);
  and and_4 (and_4_out, shift_register_4_q7[7], not_6_out);
  Shift_Register shift_register_5 (
    .shift(in_16), .in(demultiplexer_1_out3), .clk(and_1_out), .q0(shift_register_5_q7[7]),
    .q1(shift_register_5_q7[6]), .q2(shift_register_5_q7[5]), .q3(shift_register_5_q7[4]),
    .q4(shift_register_5_q7[3]), .q5(shift_register_5_q7[2]), .q6(shift_register_5_q7[1]),
    .q7(shift_register_5_q7[0]));  // open: out, load, clr, d0, d1, d2, d3, d4, d5, d6, d7
  and and_5 (and_5_out, shift_register_5_q7[7], shift_register_5_q7[6]);
  Hex_Digit_Display hex_digit_display_1 (.value({2'b00, register_2_q[7:6]}));  // open: dp
  Register register_2 (.D(shift_register_2_q7), .Q(register_2_q), .clk(and_2_out), .clr(in_12));  // open: en
  Register register_3 (.D(shift_register_3_q7), .Q(register_3_q), .clk(and_3_out), .clr(in_12));  // open: en
  Register register_4 (.D(shift_register_4_q7), .Q(register_4_q), .clk(and_4_out), .clr(in_12));  // open: en
  Register register_5 (.D(shift_register_5_q7), .Q(register_5_q), .clk(and_5_out), .clr(in_12));  // open: en
  Hex_Digit_Display hex_digit_display_2 (.value(register_2_q[3:0]));  // open: dp
  Hex_Digit_Display hex_digit_display_3 (.value(register_3_q[3:0]));  // open: dp
  Hex_Digit_Display hex_digit_display_4 (.value({2'b00, register_3_q[7:6]}));  // open: dp
  Hex_Digit_Display hex_digit_display_5 (.value({2'b00, register_4_q[7:6]}));  // open: dp
  Hex_Digit_Display hex_digit_display_6 (.value(register_4_q[3:0]));  // open: dp
  Hex_Digit_Display hex_digit_display_7 (.value({2'b00, register_5_q[7:6]}));  // open: dp
  Hex_Digit_Display hex_digit_display_8 (.value(register_5_q[3:0]));  // open: dp

  assign in_7 = in_2;
  assign in_8 = in_2;
endmodule
