// Logisim project DAAC PR1_4.circ as structural Verilog: 1 circuit, main circuit main
module main (
  input  in_1,
  input  destino,
  input  Fuente,
  input  in_4,
  input  Dato,
  input  destino_2,
  input  Fuente_2,
  input  in_8,
  input  in_9,
  input  in_10,
  input  in_11,
  input  in_12,
  input  in_13,
  input  in_14,
  input  in_15,
  input  in_16,
  input  Dato_2,
  input  in_18,
  input  in_19,
  input  in_20,
  input  in_21,
  input  destino_3,
  input  Fuente_3,
  input  in_24,
  input  Dato_3,
  input  destino_4,
  input  Fuente_4,
  input  in_28,
  input  in_29,
  input  in_30,
  input  in_31,
  input  in_32,
  input  in_33,
  input  in_34,
  input  Dato_4,
  input  in_36,
  input  in_37,
  input  in_38,
  input  in_39
);

  wire and_1_out, and_2_out, and_3_out, and_4_out, and_5_out, clock_1_out, controlled_buffer_1_out,
       demultiplexer_1_out0, demultiplexer_1_out1, demultiplexer_1_out2, demultiplexer_1_out3, not_1_out,
       not_2_out, not_3_out, not_4_out, not_5_out, not_6_out, not_7_out, or_1_out, or_2_out, or_3_out,
       or_4_out, shift_register_1_out, shift_register_2_out, shift_register_3_out, shift_register_4_out;
  wire [1:0] multiplexer_1_out;
  wire [3:0] counter_1_q;
  wire [7:0] register_1_q, register_2_q, register_3_q, register_4_q, shift_register_1_q7,
       shift_register_2_q7, shift_register_3_q7, shift_register_4_q7;

  Shift_Register shift_register_1 (
    .shift(or_1_out), .in(controlled_buffer_1_out), .clk(and_3_out), .out(shift_register_1_out), .load(in_1),
    .d0(destino), .q0(shift_register_1_q7[7]), .d1(Fuente), .q1(shift_register_1_q7[6]), .d2(in_4),
    .q2(shift_register_1_q7[5]), .d3(Dato), .q3(shift_register_1_q7[4]), .d4(in_8),
    .q4(shift_register_1_q7[3]), .d5(in_9), .q5(shift_register_1_q7[2]), .d6(in_10),
    .q6(shift_register_1_q7[1]), .d7(in_11), .q7(shift_register_1_q7[0]));  // open: clr
  and and_1 (and_1_out, shift_register_1_q7[7], shift_register_1_q7[6], not_1_out, counter_1_q[3]);
  Shift_Register shift_register_2 (
    .shift(or_3_out), .in(controlled_buffer_1_out), .clk(and_3_out), .out(shift_register_2_out), .load(in_1),
    .d0(destino_3), .q0(shift_register_2_q7[7]), .d1(Fuente_3), .q1(shift_register_2_q7[6]), .d2(in_24),
    .q2(shift_register_2_q7[5]), .d3(Dato_3), .q3(shift_register_2_q7[4]), .d4(in_28),
    .q4(shift_register_2_q7[3]), .d5(in_29), .q5(shift_register_2_q7[2]), .d6(in_30),
    .q6(shift_register_2_q7[1]), .d7(in_31), .q7(shift_register_2_q7[0]));  // open: clr
  and and_2 (and_2_out, shift_register_2_q7[7], shift_register_2_q7[6], not_2_out, counter_1_q[3]);
  not not_1 (not_1_out, in_20);
  not not_2 (not_2_out, in_38);
  Register register_1 (.D(shift_register_1_q7), .Q(register_1_q), .clk(and_1_out));  // open: en, clr
  assign controlled_buffer_1_out = in_20 ? shift_register_1_out : 1'bz;  // Controlled_Buffer controlled_buffer_1
  Register register_2 (.D(shift_register_2_q7), .Q(register_2_q), .clk(and_2_out));  // open: en, clr
  assign controlled_buffer_1_out = in_38 ? shift_register_2_out : 1'bz;  // Controlled_Buffer controlled_buffer_2
  Hex_Digit_Display hex_digit_display_1 (.value(register_1_q[7:4]));  // open: dp
  Hex_Digit_Display hex_digit_display_2 (.value(register_1_q[3:0]));  // open: dp
  Hex_Digit_Display hex_digit_display_3 (.value(register_2_q[3:0]));  // open: dp
  Hex_Digit_Display hex_digit_display_4 (.value(register_2_q[7:4]));  // open: dp
  Counter #(.width(4), .max('hf)) counter_1 (
    .Q(counter_1_q), .clk(and_3_out), .clr(in_1));  // open: load, D, count, carry
  Clock clock_1 (.out(clock_1_out));
  not not_3 (not_3_out, counter_1_q[3]);
  and and_3 (and_3_out, clock_1_out, not_3_out);
  Shift_Register shift_register_3 (
    .shift(or_2_out), .in(controlled_buffer_1_out), .clk(and_3_out), .out(shift_register_3_out), .load(in_1),
    .d0(destino_2), .q0(shift_register_3_q7[7]), .d1(Fuente_2), .q1(shift_register_3_q7[6]), .d2(in_12),
    .q2(shift_register_3_q7[5]), .d3(in_13), .q3(shift_register_3_q7[4]), .d4(in_16),
    .q4(shift_register_3_q7[3]), .d5(Dato_2), .q5(shift_register_3_q7[2]), .d6(in_18),
    .q6(shift_register_3_q7[1]), .d7(in_19), .q7(shift_register_3_q7[0]));  // open: clr
  not not_4 (not_4_out, shift_register_3_q7[7]);
  and and_4 (and_4_out, not_4_out, shift_register_3_q7[6], counter_1_q[3], not_6_out);
  Shift_Register shift_register_4 (
    .shift(or_4_out), .in(controlled_buffer_1_out), .clk(and_3_out), .out(shift_register_4_out), .load(in_1),
    .d0(destino_4), .q0(shift_register_4_q7[7]), .d1(Fuente_4), .q1(shift_register_4_q7[6]), .d2(in_32),
    .q2(shift_register_4_q7[5]), .d3(in_33), .q3(shift_register_4_q7[4]), .d4(in_34),
    .q4(shift_register_4_q7[3]), .d5(Dato_4), .q5(shift_register_4_q7[2]), .d6(in_36),
    .q6(shift_register_4_q7[1]), .d7(in_37), .q7(shift_register_4_q7[0]));  // open: clr
  not not_5 (not_5_out, shift_register_4_q7[7]);
  and and_5 (and_5_out, not_5_out, shift_register_4_q7[6], counter_1_q[3], not_7_out);
  assign controlled_buffer_1_out = in_21 ? shift_register_3_out : 1'bz;  // Controlled_Buffer controlled_buffer_3
  not not_6 (not_6_out, in_21);
  assign controlled_buffer_1_out = in_39 ? shift_register_4_out : 1'bz;  // Controlled_Buffer controlled_buffer_4
  not not_7 (not_7_out, in_39);
  Hex_Digit_Display hex_digit_display_5 (.value(register_3_q[7:4]));  // open: dp
  Register register_3 (.D(shift_register_3_q7), .Q(register_3_q), .clk(and_4_out));  // open: en, clr
  Hex_Digit_Display hex_digit_display_6 (.value(register_4_q[7:4]));  // open: dp
  Register register_4 (.D(shift_register_4_q7), .Q(register_4_q), .clk(and_5_out));  // open: en, clr
  Hex_Digit_Display hex_digit_display_7 (.value(register_3_q[3:0]));  // open: dp
  Hex_Digit_Display hex_digit_display_8 (.value(register_4_q[3:0]));  // open: dp
  or or_1 (or_1_out, in_20, demultiplexer_1_out0);
  or or_2 (or_2_out, in_21, demultiplexer_1_out1);
  or or_3 (or_3_out, in_38, demultiplexer_1_out2);
  or or_4 (or_4_out, in_39, demultiplexer_1_out3);
  Demultiplexer #(.select(2), .disabled(0)) demultiplexer_1 (
    .out0(demultiplexer_1_out0), .out1(demultiplexer_1_out1), .out2(demultiplexer_1_out2),
    .out3(demultiplexer_1_out3), .in(1'b1), .sel(multiplexer_1_out), .en(1'b1));
  Multiplexer #(.select(2), .width(2)) multiplexer_1 (
    .in0({Fuente_4, destino_4}), .in1({Fuente_3, destino_3}), .in2({destino_2, Fuente_2}),
    .in3({destino, Fuente}), .out(multiplexer_1_out), .sel({in_14, in_15}), .en(1'b1));
endmodule
