// Logisim project Pr1_6MALO.circ as structural Verilog: 1 circuit, main circuit main
module main (
  input  in_1,
  input  in_2,
  input  in_3,
  input  in_4,
  input  in_5,
  input  in_6,
  input  in_7,
  input  in_8,
  input  in_9,
  input  in_10,
  input  in_11,
  input  in_12,
  input  in_13
);

  wire and_1_out, and_2_out, and_3_out, and_4_out, and_5_out, and_6_out, and_7_out, clock_2_out,
       controlled_buffer_3_out, demultiplexer_1_out0, demultiplexer_1_out1, demultiplexer_1_out2,
       demultiplexer_1_out3, not_1_out, not_2_out, not_3_out, not_4_out, not_5_out, not_6_out, not_7_out,
       not_8_out, not_9_out, not_10_out, not_11_out, not_12_out, not_13_out, or_1_out, or_2_out, or_3_out,
       or_4_out, or_5_out, shift_register_1_out, shift_register_2_out, shift_register_3_out,
       shift_register_4_out, xor_1_out, xor_2_out, xor_3_out, xor_4_out, xor_5_out, xor_6_out, xor_7_out;
  wire [0:0] undriven;
  wire [1:0] controlled_buffer_11_out_2, counter_1_q, multiplexer_2_out;
  wire [3:0] counter_2_q;
  wire [5:0] controlled_buffer_11_out;
  wire [7:0] controlled_buffer_1_out, controlled_buffer_5_out, controlled_buffer_9_out, multiplexer_1_out,
       ram_1_data, ram_2_data, ram_3_data, ram_4_data, register_1_q, register_2_q, register_3_q,
       register_4_q, shift_register_1_q7, shift_register_2_q7, shift_register_3_q7, shift_register_4_q7;

  Clock clock_1 ();  // open: out
  Counter #(.width(2), .max('h3)) counter_1 (
    .Q(counter_1_q), .clk(and_3_out), .clr(in_2));  // open: load, D, count, carry
  not not_1 (not_1_out, in_5);
  Shift_Register #(.length(9)) shift_register_1 (
    .in(controlled_buffer_3_out), .clk(and_5_out), .out(shift_register_1_out), .load(in_4),
    .d0(controlled_buffer_1_out[7]), .q0(shift_register_1_q7[7]), .d1(controlled_buffer_1_out[6]),
    .q1(shift_register_1_q7[6]), .d2(controlled_buffer_1_out[5]), .q2(shift_register_1_q7[5]),
    .d3(controlled_buffer_1_out[4]), .q3(shift_register_1_q7[4]), .d4(controlled_buffer_1_out[3]),
    .q4(shift_register_1_q7[3]), .d5(controlled_buffer_1_out[2]), .q5(shift_register_1_q7[2]),
    .d6(controlled_buffer_1_out[1]), .q6(shift_register_1_q7[1]), .d7(controlled_buffer_1_out[0]),
    .q7(shift_register_1_q7[0]), .d8(undriven[0]));  // open: shift, clr, q8
  not not_2 (not_2_out, shift_register_1_q7[7]);
  Shift_Register shift_register_2 (
    .shift(or_4_out), .in(controlled_buffer_3_out), .clk(and_5_out), .out(shift_register_2_out), .load(in_4),
    .d0(controlled_buffer_5_out[7]), .q0(shift_register_2_q7[7]), .d1(controlled_buffer_5_out[6]),
    .q1(shift_register_2_q7[6]), .d2(controlled_buffer_5_out[5]), .q2(shift_register_2_q7[5]),
    .d3(controlled_buffer_5_out[4]), .q3(shift_register_2_q7[4]), .d4(controlled_buffer_5_out[3]),
    .q4(shift_register_2_q7[3]), .d5(controlled_buffer_5_out[2]), .q5(shift_register_2_q7[2]),
    .d6(controlled_buffer_5_out[1]), .q6(shift_register_2_q7[1]), .d7(controlled_buffer_5_out[0]),
    .q7(shift_register_2_q7[0]));  // open: clr
  not not_3 (not_3_out, in_12);
  Multiplexer #(.select(2), .width(8)) multiplexer_1 (.out(multiplexer_1_out));  // open: in0, in1, in2, in3, sel, en
  RAM #(.addrWidth(2)) ram_1 (
    .addr(counter_1_q), .data(ram_1_data), .sel(1'b1), .clk(and_3_out), .ld(in_5), .clr(in_1));
  not not_4 (not_4_out, in_8);
  not not_5 (not_5_out, shift_register_1_q7[6]);
  and and_1 (and_1_out, not_2_out, not_5_out, not_4_out, counter_2_q[3]);
  not not_6 (not_6_out, in_10);
  not not_7 (not_7_out, shift_register_2_q7[6]);
  and and_2 (and_2_out, shift_register_2_q7[7], not_7_out, not_6_out, counter_2_q[3]);
  assign controlled_buffer_1_out = in_5 ? ram_1_data : 8'bz;  // Controlled_Buffer controlled_buffer_1
  assign ram_1_data = not_1_out ? shift_register_1_q7 : 8'bz;  // Controlled_Buffer controlled_buffer_2
  assign controlled_buffer_3_out = in_8 ? shift_register_1_out : 1'bz;  // Controlled_Buffer controlled_buffer_3
  assign controlled_buffer_3_out = in_10 ? shift_register_2_out : 1'bz;  // Controlled_Buffer controlled_buffer_4
  RAM #(.addrWidth(2)) ram_2 (
    .addr(counter_1_q), .data(ram_2_data), .sel(1'b1), .clk(and_3_out), .ld(in_12), .clr(in_1));
  xor xor_1 (xor_1_out, multiplexer_1_out[0], multiplexer_1_out[1]);
  xor xor_2 (xor_2_out, multiplexer_1_out[2], multiplexer_1_out[3]);
  xor xor_3 (xor_3_out, multiplexer_1_out[4], multiplexer_1_out[5]);
  xor xor_4 (xor_4_out, multiplexer_1_out[6], multiplexer_1_out[7]);
  Hex_Digit_Display hex_digit_display_1 (.value(register_1_q[7:4]));  // open: dp
  Register register_1 (.D(shift_register_1_q7), .Q(register_1_q), .clk(and_1_out));  // open: en, clr
  Hex_Digit_Display hex_digit_display_2 (.value(register_2_q[7:4]));  // open: dp
  Register register_2 (.D(shift_register_2_q7), .Q(register_2_q), .clk(and_2_out));  // open: en, clr
  assign controlled_buffer_5_out = in_12 ? ram_2_data : 8'bz;  // Controlled_Buffer controlled_buffer_5
  assign ram_2_data = not_3_out ? shift_register_2_q7 : 8'bz;  // Controlled_Buffer controlled_buffer_6
  xor xor_5 (xor_5_out, xor_1_out, xor_2_out);
  xor xor_6 (xor_6_out, xor_3_out, xor_4_out);
  Hex_Digit_Display hex_digit_display_3 (.value(register_1_q[3:0]));  // open: dp
  Hex_Digit_Display hex_digit_display_4 (.value(register_2_q[3:0]));  // open: dp
  xor xor_7 (xor_7_out, xor_5_out, xor_6_out);
  and and_3 (and_3_out, and_4_out, clock_2_out);
  and and_4 (and_4_out, ~in_4, or_1_out);  // AND_Gate
  Counter #(.width(4), .max('hf)) counter_2 (
    .Q(counter_2_q), .clk(and_5_out), .clr(or_1_out));  // open: load, D, count, carry
  Clock clock_2 (.out(clock_2_out));
  or or_1 (or_1_out, in_4, counter_2_q[3]);
  not not_8 (not_8_out, counter_2_q[3]);
  and and_5 (and_5_out, clock_2_out, not_8_out);
  Shift_Register shift_register_3 (
    .shift(or_3_out), .in(controlled_buffer_3_out), .clk(and_5_out), .out(shift_register_3_out), .load(in_4),
    .d0(controlled_buffer_9_out[7]), .q0(shift_register_3_q7[7]), .d1(controlled_buffer_9_out[6]),
    .q1(shift_register_3_q7[6]), .d2(controlled_buffer_9_out[5]), .q2(shift_register_3_q7[5]),
    .d3(controlled_buffer_9_out[4]), .q3(shift_register_3_q7[4]), .d4(controlled_buffer_9_out[3]),
    .q4(shift_register_3_q7[3]), .d5(controlled_buffer_9_out[2]), .q5(shift_register_3_q7[2]),
    .d6(controlled_buffer_9_out[1]), .q6(shift_register_3_q7[1]), .d7(controlled_buffer_9_out[0]),
    .q7(shift_register_3_q7[0]));  // open: clr
  not not_9 (not_9_out, shift_register_3_q7[7]);
  and and_6 (and_6_out, not_9_out, shift_register_3_q7[6], counter_2_q[3], not_11_out);
  Shift_Register shift_register_4 (
    .shift(or_5_out), .in(controlled_buffer_3_out), .clk(and_5_out), .out(shift_register_4_out), .load(in_4),
    .d0(controlled_buffer_11_out_2[0]), .q0(shift_register_4_q7[7]), .d1(controlled_buffer_11_out_2[1]),
    .q1(shift_register_4_q7[6]), .d2(controlled_buffer_11_out[5]), .q2(shift_register_4_q7[5]),
    .d3(controlled_buffer_11_out[4]), .q3(shift_register_4_q7[4]), .d4(controlled_buffer_11_out[3]),
    .q4(shift_register_4_q7[3]), .d5(controlled_buffer_11_out[2]), .q5(shift_register_4_q7[2]),
    .d6(controlled_buffer_11_out[1]), .q6(shift_register_4_q7[1]), .d7(controlled_buffer_11_out[0]),
    .q7(shift_register_4_q7[0]));  // open: clr
  and and_7 (and_7_out, shift_register_4_q7[7], shift_register_4_q7[6], counter_2_q[3], not_12_out);
  not not_10 (not_10_out, in_13);
  not not_11 (not_11_out, in_9);
  not not_12 (not_12_out, in_11);
  RAM #(.addrWidth(2)) ram_3 (
    .addr(counter_1_q), .data(ram_3_data), .sel(1'b1), .clk(and_3_out), .ld(in_3), .clr(in_1));
  not not_13 (not_13_out, in_3);
  assign controlled_buffer_3_out = in_9 ? shift_register_3_out : 1'bz;  // Controlled_Buffer controlled_buffer_7
  assign controlled_buffer_3_out = in_11 ? shift_register_4_out : 1'bz;  // Controlled_Buffer controlled_buffer_8
  RAM #(.addrWidth(2)) ram_4 (
    .addr(counter_1_q), .data(ram_4_data), .sel(1'b1), .clk(and_3_out), .ld(in_13), .clr(in_1));
  assign controlled_buffer_9_out = in_3 ? ram_3_data : 8'bz;  // Controlled_Buffer controlled_buffer_9
  assign ram_3_data = not_13_out ? register_3_q : 8'bz;  // Controlled_Buffer controlled_buffer_10
  Register register_3 (.D(shift_register_3_q7), .Q(register_3_q), .clk(and_6_out));  // open: en, clr
  Hex_Digit_Display hex_digit_display_5 (.value(register_4_q[3:0]));  // open: dp
  Hex_Digit_Display hex_digit_display_6 (.value(register_4_q[7:4]));  // open: dp
  Register register_4 (.D(shift_register_4_q7), .Q(register_4_q), .clk(and_7_out));  // open: en, clr
  assign {controlled_buffer_11_out_2[0], controlled_buffer_11_out_2[1], controlled_buffer_11_out} = in_13 ? ram_4_data : 8'bz;  // Controlled_Buffer controlled_buffer_11
  assign ram_4_data = not_10_out ? shift_register_4_q7 : 8'bz;  // Controlled_Buffer controlled_buffer_12
  Hex_Digit_Display hex_digit_display_7 (.value(register_3_q[7:4]));  // open: dp
  Hex_Digit_Display hex_digit_display_8 (.value(register_3_q[3:0]));  // open: dp
  or or_2 (or_2_out, in_8, demultiplexer_1_out0);
  or or_3 (or_3_out, in_9, demultiplexer_1_out1);
  or or_4 (or_4_out, in_10, demultiplexer_1_out2);
  or or_5 (or_5_out, in_11, demultiplexer_1_out3);
  Multiplexer #(.select(2), .width(2)) multiplexer_2 (
    .in0(controlled_buffer_11_out_2), .in1({controlled_buffer_5_out[6], controlled_buffer_5_out[7]}),
    .in2(controlled_buffer_9_out[7:6]), .in3(controlled_buffer_1_out[7:6]), .out(multiplexer_2_out),
    .sel({in_6, in_7}), .en(1'b1));
  Demultiplexer #(.select(2), .disabled(0)) demultiplexer_1 (
    .out0(demultiplexer_1_out0), .out1(demultiplexer_1_out1), .out2(demultiplexer_1_out2),
    .out3(demultiplexer_1_out3), .in(1'b1), .sel(multiplexer_2_out), .en(1'b1));
endmodule
