// Logisim project Pr1_7.circ as structural Verilog: 1 circuit, main circuit main
module main (
  input  in_1,
  input  in_2,
  input  in_3,
  input  in_4,
  input  in_5,
  input  in_6
);

  wire and_1_out, and_2_out, and_3_out, and_4_out, and_5_out, and_7_out, and_8_out, clock_1_out,
       controlled_buffer_3_out, demultiplexer_1_out0, demultiplexer_1_out1, demultiplexer_1_out2,
       demultiplexer_1_out3, not_1_out, not_2_out, not_3_out, not_5_out, not_6_out, not_7_out, not_8_out,
       not_9_out, not_10_out, not_11_out, not_12_out, not_13_out, not_14_out, or_1_out, or_2_out, or_3_out,
       or_4_out, or_5_out, or_6_out, Paridad, R8, register_5_q, shift_register_1_out, shift_register_2_out,
       shift_register_3_out, shift_register_4_out, xor_1_out, xor_2_out, xor_3_out, xor_4_out, xor_5_out,
       xor_6_out, xor_7_out, xor_8_out, xor_9_out, xor_11_out, xor_12_out, xor_13_out, xor_14_out, xor_15_out;
  wire [1:0] counter_1_q, multiplexer_4_out;
  wire [3:0] decoder_1_out0;
  wire [4:0] Pasos;
  wire [6:6] not_4_out;
  wire [7:0] multiplexer_1_out, multiplexer_2_out, multiplexer_3_out, P1, R1, R2, R3, R4, ram_1_data,
       ram_2_data, ram_3_data, ram_4_data, register_1_q, register_3_q, register_6_q, register_8_q,
       shift_register_1_q7, shift_register_2_q7, shift_register_3_q7, shift_register_4_q7;

  Counter #(.width(2), .max('h3)) counter_1 (
    .Q(counter_1_q), .clk(and_3_out), .clr(in_4));  // open: load, D, count, carry
  not not_1 (not_1_out, decoder_1_out0[0]);
  Multiplexer #(.select(2), .width(8)) multiplexer_1 (
    .in0(P1), .in1(P1), .in2(P1), .in3(P1), .out(multiplexer_1_out), .sel({in_1, in_2}));  // open: en
  Multiplexer #(.select(2), .width(8)) multiplexer_2 (
    .in0(R1), .in1(R2), .in2(R3), .in3(R4), .out(multiplexer_2_out), .sel({in_1, in_2}));  // open: en
  Shift_Register #(.length(9)) shift_register_1 (
    .shift(or_3_out), .in(controlled_buffer_3_out), .clk(and_5_out), .out(shift_register_1_out),
    .load(or_1_out), .d0(P1[7]), .q0(shift_register_1_q7[7]), .d1(P1[6]), .q1(shift_register_1_q7[6]),
    .d2(P1[5]), .q2(shift_register_1_q7[5]), .d3(P1[4]), .q3(shift_register_1_q7[4]), .d4(P1[3]),
    .q4(shift_register_1_q7[3]), .d5(P1[2]), .q5(shift_register_1_q7[2]), .d6(P1[1]),
    .q6(shift_register_1_q7[1]), .d7(P1[0]), .q7(shift_register_1_q7[0]), .d8(Paridad));  // open: clr, q8
  not not_2 (not_2_out, shift_register_1_q7[7]);
  Shift_Register #(.length(9)) shift_register_2 (
    .shift(or_5_out), .in(controlled_buffer_3_out), .clk(and_5_out), .out(shift_register_2_out),
    .load(or_1_out), .d0(P1[7]), .q0(shift_register_2_q7[7]), .d1(P1[6]), .q1(shift_register_2_q7[6]),
    .d2(P1[5]), .q2(shift_register_2_q7[5]), .d3(P1[4]), .q3(shift_register_2_q7[4]), .d4(P1[3]),
    .q4(shift_register_2_q7[3]), .d5(P1[2]), .q5(shift_register_2_q7[2]), .d6(P1[1]),
    .q6(shift_register_2_q7[1]), .d7(P1[0]), .q7(shift_register_2_q7[0]), .d8(Paridad));  // open: clr, q8
  not not_3 (not_3_out, decoder_1_out0[2]);
  xor xor_1 (xor_1_out, multiplexer_1_out[0], multiplexer_1_out[1]);
  xor xor_2 (xor_2_out, xor_1_out, multiplexer_1_out[2]);
  Multiplexer #(.width(8), .enable("false")) multiplexer_3 (
    .in0(multiplexer_2_out), .in1({multiplexer_2_out[7], not_4_out[6], multiplexer_2_out[5:0]}),
    .out(multiplexer_3_out), .sel(in_6));
  not not_4 (not_4_out[6], multiplexer_2_out[6]);
  RAM #(.addrWidth(2)) ram_1 (
    .addr(counter_1_q), .data(ram_1_data), .sel(1'b1), .clk(and_3_out), .ld(decoder_1_out0[0]), .clr(in_3));
  not not_5 (not_5_out, decoder_1_out0[0]);
  not not_6 (not_6_out, shift_register_1_q7[6]);
  and and_1 (and_1_out, not_2_out, not_6_out, not_5_out, R8);
  not not_7 (not_7_out, decoder_1_out0[2]);
  not not_8 (not_8_out, shift_register_2_q7[6]);
  and and_2 (and_2_out, shift_register_2_q7[7], not_8_out, not_7_out, R8);
  xor xor_3 (xor_3_out, xor_2_out, multiplexer_1_out[3]);
  assign P1 = decoder_1_out0[0] ? ram_1_data : 8'bz;  // Controlled_Buffer controlled_buffer_1
  assign ram_1_data = not_1_out ? shift_register_1_q7 : 8'bz;  // Controlled_Buffer controlled_buffer_2
  assign controlled_buffer_3_out = decoder_1_out0[0] ? shift_register_1_out : 1'bz;  // Controlled_Buffer controlled_buffer_3
  assign controlled_buffer_3_out = decoder_1_out0[2] ? shift_register_2_out : 1'bz;  // Controlled_Buffer controlled_buffer_4
  RAM #(.addrWidth(2)) ram_2 (
    .addr(counter_1_q), .data(ram_2_data), .sel(1'b1), .clk(and_3_out), .ld(decoder_1_out0[2]), .clr(in_3));
  xor xor_4 (xor_4_out, xor_3_out, multiplexer_1_out[4]);
  xor xor_5 (xor_5_out, xor_4_out, multiplexer_1_out[5]);
  xor xor_6 (xor_6_out, multiplexer_3_out[0], multiplexer_3_out[1]);
  xor xor_7 (xor_7_out, xor_6_out, multiplexer_3_out[2]);
  Hex_Digit_Display hex_digit_display_1 (.value(register_1_q[7:4]));  // open: dp
  Register register_1 (.D(shift_register_1_q7), .Q(register_1_q), .clk(and_1_out));  // open: en, clr
  Register register_2 (.D(shift_register_1_q7), .Q(R1), .clk(in_5));  // open: en, clr
  Hex_Digit_Display hex_digit_display_2 (.value(register_3_q[7:4]));  // open: dp
  Register register_3 (.D(shift_register_2_q7), .Q(register_3_q), .clk(and_2_out));  // open: en, clr
  assign P1 = decoder_1_out0[2] ? ram_2_data : 8'bz;  // Controlled_Buffer controlled_buffer_5
  assign ram_2_data = not_3_out ? shift_register_2_q7 : 8'bz;  // Controlled_Buffer controlled_buffer_6
  xor xor_8 (xor_8_out, xor_5_out, multiplexer_1_out[6]);
  xor xor_9 (xor_9_out, xor_7_out, multiplexer_3_out[3]);
  Hex_Digit_Display hex_digit_display_3 (.value(register_1_q[3:0]));  // open: dp
  Hex_Digit_Display hex_digit_display_4 (.value(register_3_q[3:0]));  // open: dp
  Register register_4 (.D(shift_register_2_q7), .Q(R3), .clk(in_5));  // open: en, clr
  xor xor_10 (Paridad, xor_8_out, multiplexer_1_out[7]);
  xor xor_11 (xor_11_out, xor_9_out, multiplexer_3_out[4]);
  xor xor_12 (xor_12_out, xor_11_out, multiplexer_3_out[5]);
  or or_1 (or_1_out, register_5_q, in_5);
  xor xor_13 (xor_13_out, xor_12_out, multiplexer_3_out[6]);
  and and_3 (and_3_out, and_4_out, clock_1_out);
  and and_4 (and_4_out, ~or_1_out, or_2_out);  // AND_Gate
  Counter #(.width(5), .max('h1f)) counter_2 (
    .Q(Pasos), .clk(and_5_out), .clr(or_2_out));  // open: load, D, count, carry
  Clock clock_1 (.out(clock_1_out));
  or or_2 (or_2_out, or_1_out, R8);
  xor xor_14 (xor_14_out, Paridad, xor_15_out);
  xor xor_15 (xor_15_out, xor_13_out, multiplexer_3_out[7]);
  not not_9 (not_9_out, R8);
  and and_5 (and_5_out, clock_1_out, not_9_out);
  and and_6 (R8, Pasos[0], ~Pasos[1], ~Pasos[2], Pasos[3], ~Pasos[4]);  // AND_Gate
  Register #(.width(1)) register_5 (.D(xor_14_out), .Q(register_5_q), .clk(clock_1_out), .clr(in_5));  // open: en
  Shift_Register #(.length(9)) shift_register_3 (
    .shift(or_4_out), .in(controlled_buffer_3_out), .clk(and_5_out), .out(shift_register_3_out),
    .load(or_1_out), .d0(P1[7]), .q0(shift_register_3_q7[7]), .d1(P1[6]), .q1(shift_register_3_q7[6]),
    .d2(P1[5]), .q2(shift_register_3_q7[5]), .d3(P1[4]), .q3(shift_register_3_q7[4]), .d4(P1[3]),
    .q4(shift_register_3_q7[3]), .d5(P1[2]), .q5(shift_register_3_q7[2]), .d6(P1[1]),
    .q6(shift_register_3_q7[1]), .d7(P1[0]), .q7(shift_register_3_q7[0]), .d8(Paridad));  // open: clr, q8
  not not_10 (not_10_out, shift_register_3_q7[7]);
  and and_7 (and_7_out, not_10_out, shift_register_3_q7[6], R8, not_12_out);
  Shift_Register #(.length(9)) shift_register_4 (
    .shift(or_6_out), .in(controlled_buffer_3_out), .clk(and_5_out), .out(shift_register_4_out),
    .load(or_1_out), .d0(P1[7]), .q0(shift_register_4_q7[7]), .d1(P1[6]), .q1(shift_register_4_q7[6]),
    .d2(P1[5]), .q2(shift_register_4_q7[5]), .d3(P1[4]), .q3(shift_register_4_q7[4]), .d4(P1[3]),
    .q4(shift_register_4_q7[3]), .d5(P1[2]), .q5(shift_register_4_q7[2]), .d6(P1[1]),
    .q6(shift_register_4_q7[1]), .d7(P1[0]), .q7(shift_register_4_q7[0]), .d8(Paridad));  // open: clr, q8
  and and_8 (and_8_out, shift_register_4_q7[7], shift_register_4_q7[6], R8, not_13_out);
  not not_11 (not_11_out, decoder_1_out0[3]);
  not not_12 (not_12_out, decoder_1_out0[1]);
  not not_13 (not_13_out, decoder_1_out0[3]);
  RAM #(.addrWidth(2)) ram_3 (
    .addr(counter_1_q), .data(ram_3_data), .sel(1'b1), .clk(and_3_out), .ld(decoder_1_out0[1]), .clr(in_3));
  not not_14 (not_14_out, decoder_1_out0[1]);
  assign controlled_buffer_3_out = decoder_1_out0[1] ? shift_register_3_out : 1'bz;  // Controlled_Buffer controlled_buffer_7
  assign controlled_buffer_3_out = decoder_1_out0[3] ? shift_register_4_out : 1'bz;  // Controlled_Buffer controlled_buffer_8
  RAM #(.addrWidth(2)) ram_4 (
    .addr(counter_1_q), .data(ram_4_data), .sel(1'b1), .clk(and_3_out), .ld(decoder_1_out0[3]), .clr(in_3));
  assign P1 = decoder_1_out0[1] ? ram_3_data : 8'bz;  // Controlled_Buffer controlled_buffer_9
  assign ram_3_data = not_14_out ? register_6_q : 8'bz;  // Controlled_Buffer controlled_buffer_10
  Register register_6 (.D(shift_register_3_q7), .Q(register_6_q), .clk(and_7_out));  // open: en, clr
  Register register_7 (.D(shift_register_3_q7), .Q(R2), .clk(in_5));  // open: en, clr
  Hex_Digit_Display hex_digit_display_5 (.value(register_8_q[7:4]));  // open: dp
  Hex_Digit_Display hex_digit_display_6 (.value(register_8_q[3:0]));  // open: dp
  Register register_8 (.D(shift_register_4_q7), .Q(register_8_q), .clk(and_8_out));  // open: en, clr
  assign P1 = decoder_1_out0[3] ? ram_4_data : 8'bz;  // Controlled_Buffer controlled_buffer_11
  assign ram_4_data = not_11_out ? shift_register_4_q7 : 8'bz;  // Controlled_Buffer controlled_buffer_12
  Hex_Digit_Display hex_digit_display_7 (.value(register_6_q[3:0]));  // open: dp
  Hex_Digit_Display hex_digit_display_8 (.value(register_6_q[7:4]));  // open: dp
  Register register_9 (.D(shift_register_4_q7), .Q(R4), .clk(in_5));  // open: en, clr
  or or_3 (or_3_out, decoder_1_out0[0], demultiplexer_1_out0);
  or or_4 (or_4_out, decoder_1_out0[1], demultiplexer_1_out1);
  or or_5 (or_5_out, decoder_1_out0[2], demultiplexer_1_out2);
  or or_6 (or_6_out, decoder_1_out0[3], demultiplexer_1_out3);
  Multiplexer #(.select(2), .width(2)) multiplexer_4 (
    .in0({P1[6], P1[7]}), .in1({P1[6], P1[7]}), .in2(P1[7:6]), .in3(P1[7:6]), .out(multiplexer_4_out),
    .sel(P1[7:6]), .en(1'b1));
  Demultiplexer #(.select(2), .disabled(0)) demultiplexer_1 (
    .out0(demultiplexer_1_out0), .out1(demultiplexer_1_out1), .out2(demultiplexer_1_out2),
    .out3(demultiplexer_1_out3), .in(1'b1), .sel(multiplexer_4_out), .en(1'b1));
  Decoder #(.select(2), .enable("false")) decoder_1 (
    .out0(decoder_1_out0[0]), .out1(decoder_1_out0[1]), .out2(decoder_1_out0[2]), .out3(decoder_1_out0[3]),
    .sel({in_1, in_2}));

  // Other names for the same wires on the sheet: P2[7:0] = P1; P3[7:0] = P1; P4[7:0] = P1
endmodule
