// Logisim project DAAC PR2_1.circ as structural Verilog: 1 circuit, main circuit main
module main (
  input  in_1,
  input  in_2,
  input  Datos_de_entrada,
  input  in_4,
  input  in_5,
  input  in_6,
  input  in_7,
  input  in_8,
  input  in_9,
  input  in_10,
  input  in_11,
  input  in_12,
  input  in_13,
  input  in_14,
  input  R_W,
  input  CS,
  input  OE,
  input  CLEAR,
  input  in_19,
  output out_20,
  output out_21,
  output out_22,
  output out_23,
  output out_24,
  output out_25,
  output out_26,
  output out_27
);

  wire not_1_out;
  wire [7:0] controlled_buffer_1_out, controlled_buffer_2_out;

  assign controlled_buffer_1_out = not_1_out ? {in_1, in_2, Datos_de_entrada, in_4, in_5, in_6, in_7, in_8} : 8'bz;  // Controlled_Buffer controlled_buffer_1
  assign controlled_buffer_2_out = OE ? controlled_buffer_1_out : 8'bz;  // Controlled_Buffer controlled_buffer_2
  RAM #(.addrWidth(4)) ram_1 (
    .addr({in_12, in_11, in_10, in_9}), .data(controlled_buffer_1_out), .sel(CS), .clk(R_W), .ld(OE),
    .clr(CLEAR));
  not not_1 (not_1_out, OE);
  Register Registro_Externo (
    .D(controlled_buffer_2_out), .Q({out_27, out_26, out_25, out_24, out_23, out_22, out_21, out_20}),
    .clk(in_14));  // open: en, clr
  Hex_Digit_Display hex_digit_display_1 (.value(controlled_buffer_1_out[3:0]), .dp(in_19));
  Hex_Digit_Display hex_digit_display_2 (.value(controlled_buffer_1_out[7:4]), .dp(in_19));
  Hex_Digit_Display hex_digit_display_3 (.value({out_23, out_22, out_21, out_20}), .dp(in_13));
  Hex_Digit_Display hex_digit_display_4 (.value({out_27, out_26, out_25, out_24}), .dp(in_13));

  // Notes on the sheet:
  //   Bus de direcciones
  //   Bus de datos (dato)
  //   Datos de salida
endmodule
