// Logisim project DAAC PR2_2.circ as structural Verilog: 1 circuit, main circuit main
module main (
  input  in_1,
  input  in_2,
  input  in_3,
  input  in_4,
  input  in_5,
  input  in_6,
  input  in_7,
  input  in_8,
  input  in_9,
  input  in_10,
  input  Carga_DIR,
  input  Control,
  input  START,
  input  SEL,
  input  IN_OUT,
  input  BUS_PRT,
  input  in_17,
  input  in_18,
  input  in_19,
  input  in_20,
  input  in_21,
  input  in_22,
  input  in_23,
  input  in_24,
  input  in_25,
  output out_26,
  output out_27,
  output out_28,
  output out_29,
  output out_30,
  output out_31,
  output out_32,
  output out_33,
  output out_34,
  output out_35,
  output out_36,
  output out_37,
  output out_38,
  output out_39,
  output out_40,
  output out_41,
  output out_42,
  output out_43,
  output out_44,
  output out_45,
  output out_46,
  output out_47,
  output out_48,
  output out_49,
  output out_50,
  output out_51,
  output out_52,
  output out_53,
  output out_54,
  output out_55,
  output out_56,
  output out_57
);

  wire and_1_out, and_2_out, and_3_out, and_4_out, and_5_out, and_6_out, and_7_out, and_8_out, and_9_out,
       and_10_out, and_11_out, and_12_out, and_13_out, and_14_out, clock_1_out, counter_1_carry, Escribe,
       not_1_out, not_3_out, not_4_out, not_5_out;
  wire [0:0] counter_1_q;
  wire [2:0] counter_1_q_2;
  wire [3:0] controlled_buffer_3_out, controlled_buffer_3_out_2;
  wire [7:0] controlled_buffer_1_out, ram_1_data, random_1_out, register_1_q, register_3_q, register_5_q,
       register_7_q;

  Clock clock_1 (.out(clock_1_out));
  Counter #(.width(4), .max('hf)) counter_1 (
    .load(Carga_DIR), .D({in_3, in_4, in_5, in_6}), .count(Control), .Q({counter_1_q_2, counter_1_q[0]}),
    .carry(counter_1_carry), .clk(and_1_out), .clr(START));
  and and_1 (and_1_out, clock_1_out, not_1_out);
  and and_2 (and_2_out, counter_1_q[0], 1'b1);
  not not_1 (not_1_out, counter_1_carry);
  RAM #(.addrWidth(4)) ram_1 (
    .addr({counter_1_q_2, counter_1_q[0]}), .data(ram_1_data), .sel(SEL), .clk(clock_1_out), .ld(and_2_out));  // open: clr
  not not_2 (Escribe, and_2_out);
  not not_3 (not_3_out, BUS_PRT);
  not not_4 (not_4_out, and_2_out);
  not not_5 (not_5_out, and_2_out);
  Hex_Digit_Display hex_digit_display_1 (.value(controlled_buffer_3_out_2), .dp(in_19));
  Hex_Digit_Display hex_digit_display_2 (.value(controlled_buffer_3_out), .dp(in_19));
  assign controlled_buffer_1_out = and_4_out ? ram_1_data : 8'bz;  // Controlled_Buffer controlled_buffer_1
  and and_3 (and_3_out, BUS_PRT, not_4_out);
  and and_4 (and_4_out, and_2_out, BUS_PRT);
  assign ram_1_data = and_3_out ? controlled_buffer_1_out : 8'bz;  // Controlled_Buffer controlled_buffer_2
  assign {controlled_buffer_3_out_2, controlled_buffer_3_out} = and_6_out ? ram_1_data : 8'bz;  // Controlled_Buffer controlled_buffer_3
  and and_5 (and_5_out, not_3_out, not_5_out);
  and and_6 (and_6_out, and_2_out, not_3_out);
  assign ram_1_data = and_5_out ? {controlled_buffer_3_out_2, controlled_buffer_3_out} : 8'bz;  // Controlled_Buffer controlled_buffer_4
  Hex_Digit_Display hex_digit_display_3 (.value(controlled_buffer_1_out[7:4]), .dp(in_2));
  Hex_Digit_Display hex_digit_display_4 (.value(controlled_buffer_1_out[3:0]), .dp(in_2));
  and and_7 (and_7_out, ~Escribe, in_17, clock_1_out);  // AND_Gate
  and and_8 (and_8_out, ~Escribe, in_24, clock_1_out);  // AND_Gate
  Random random_1 (.clk(in_1), .out(random_1_out));  // open: next, clr
  Register register_1 (.D(random_1_out), .Q(register_1_q), .clk(in_7));  // open: en, clr
  assign controlled_buffer_1_out = and_9_out ? register_1_q : 8'bz;  // Controlled_Buffer controlled_buffer_5
  and and_9 (and_9_out, in_9, Escribe);
  Register #(.trigger("falling")) register_2 (
    .D(controlled_buffer_1_out), .Q({out_40, out_38, out_36, out_34, out_32, out_30, out_28, out_26}),
    .clk(and_7_out));  // open: en, clr
  assign controlled_buffer_1_out = and_10_out ? register_3_q : 8'bz;  // Controlled_Buffer controlled_buffer_6
  Register register_3 (.D(random_1_out), .Q(register_3_q), .clk(in_20));  // open: en, clr
  and and_10 (and_10_out, in_22, Escribe);
  Register #(.trigger("falling")) register_4 (
    .D(controlled_buffer_1_out), .Q({out_56, out_54, out_52, out_50, out_48, out_46, out_44, out_42}),
    .clk(and_8_out));  // open: en, clr
  and and_11 (and_11_out, ~Escribe, in_18, clock_1_out);  // AND_Gate
  and and_12 (and_12_out, ~Escribe, in_25, clock_1_out);  // AND_Gate
  Register register_5 (.D(random_1_out), .Q(register_5_q), .clk(in_8));  // open: en, clr
  assign controlled_buffer_1_out = and_13_out ? register_5_q : 8'bz;  // Controlled_Buffer controlled_buffer_7
  and and_13 (and_13_out, in_10, Escribe);
  Register #(.trigger("falling")) register_6 (
    .D(controlled_buffer_1_out), .Q({out_41, out_39, out_37, out_35, out_33, out_31, out_29, out_27}),
    .clk(and_11_out));  // open: en, clr
  Register #(.trigger("falling")) register_7 (.D(random_1_out), .Q(register_7_q), .clk(in_21));  // open: en, clr
  assign controlled_buffer_1_out = and_14_out ? register_7_q : 8'bz;  // Controlled_Buffer controlled_buffer_8
  and and_14 (and_14_out, in_23, Escribe);
  Register #(.trigger("falling")) register_8 (
    .D(controlled_buffer_1_out), .Q({out_57, out_55, out_53, out_51, out_49, out_47, out_45, out_43}),
    .clk(and_12_out));  // open: en, clr

  // Notes on the sheet:
  //   Dirección directa
  //   Memoria RAM - Buffer
  //   Bus del Sistema
  //   Bus del externo
endmodule
