// Logisim project Practica 3.circ as structural Verilog: 1 circuit, main circuit main
module main (
  input  in_1,
  input  in_2,
  input  in_3,
  input  Leer_Escribir,
  output Fuera_de_memoria
);

  wire not_2_out;
  wire [1:0] ram_2_data;
  wire [4:0] ram_1_data;
  wire [7:0] controlled_buffer_2_out, ram_3_data, register_2_q;
  wire [21:0] register_1_q;

  Register #(.width(22)) register_1 (.Q(register_1_q), .clk(in_1));  // open: D, en, clr
  RAM #(.addrWidth(6), .dataWidth(5)) ram_1 (
    .addr(register_1_q[21:16]), .data(ram_1_data), .sel(1'b1), .ld(1'b1));  // open: clk, clr
  not not_1 (Fuera_de_memoria, ram_1_data[4]);
  RAM #(.addrWidth(2), .dataWidth(2)) ram_2 (
    .addr(register_1_q[15:14]), .data(ram_2_data), .sel(1'b1), .ld(1'b1));  // open: clk, clr
  Hex_Digit_Display hex_digit_display_1 (.value(controlled_buffer_2_out[7:4]));  // open: dp
  RAM #(.addrWidth(20)) ram_3 (
    .addr({ram_1_data[3:0], ram_2_data, register_1_q[13:0]}), .data(ram_3_data), .sel(ram_1_data[4]),
    .clk(in_2), .ld(not_2_out));  // open: clr
  assign ram_3_data = Leer_Escribir ? register_2_q : 8'bz;  // Controlled_Buffer controlled_buffer_1
  Register register_2 (.D(controlled_buffer_2_out), .Q(register_2_q), .clk(in_3));  // open: en, clr
  Hex_Digit_Display hex_digit_display_2 (.value(controlled_buffer_2_out[3:0]));  // open: dp
  assign controlled_buffer_2_out = not_2_out ? ram_3_data : 8'bz;  // Controlled_Buffer controlled_buffer_2
  not not_2 (not_2_out, Leer_Escribir);

  // Notes on the sheet:
  //   Dirección lógica de 22 bits
  //   Tabla de página de 64kb
  //   Tabla de segmento de 16kb
  //   Memoria principal de 1024KB
endmodule
