// Logisim project Practica 4.circ as structural Verilog: 1 circuit, main circuit main
module main (
  input  in_1,
  input  in_2,
  input  in_3,
  input  Leer_Escribir,
  input  [1:0] in_5,
  input  in_6,
  input  in_7,
  input  in_8,
  input  in_9,
  input  Leer_Escribir_2,
  output Tiene_permiso
);

  wire clock_1_out, not_1_out, not_2_out, not_3_out;
  wire [1:0] ram_3_data;
  wire [7:0] controlled_buffer_1_out, controlled_buffer_3_out, ram_2_data, ram_4_data, register_2_q,
       register_3_q;
  wire [8:0] ram_1_data;
  wire [13:0] counter_1_q, multiplexer_1_out;
  wire [21:0] register_1_q;

  Clock clock_1 (.out(clock_1_out));
  Register #(.width(22)) register_1 (.Q(register_1_q), .clk(in_1));  // open: D, en, clr
  Counter #(.width(14), .max('h3fff)) counter_1 (
    .count(in_6), .Q(counter_1_q), .clk(clock_1_out), .clr(in_7));  // open: load, D, carry
  RAM #(.addrWidth(6), .dataWidth(9)) ram_1 (
    .addr(register_1_q[21:16]), .data(ram_1_data), .sel(1'b1), .ld(1'b1));  // open: clk, clr
  RAM #(.addrWidth(14)) ram_2 (
    .addr(counter_1_q), .data(ram_2_data), .sel(1'b1), .clk(in_8), .ld(not_2_out));  // open: clr
  Register register_2 (.D(controlled_buffer_3_out), .Q(register_2_q), .clk(in_9));  // open: en, clr
  Multiplexer #(.width(14), .disabled(0), .enable("false")) multiplexer_1 (
    .in0(register_1_q[13:0]), .in1(counter_1_q), .out(multiplexer_1_out), .sel(not_1_out));
  not not_1 (not_1_out, ram_1_data[4]);
  assign controlled_buffer_1_out = not_2_out ? ram_2_data : 8'bz;  // Controlled_Buffer controlled_buffer_1
  not not_2 (not_2_out, Leer_Escribir_2);
  assign ram_2_data = Leer_Escribir_2 ? register_2_q : 8'bz;  // Controlled_Buffer controlled_buffer_2
  RAM #(.addrWidth(2), .dataWidth(2)) ram_3 (
    .addr(register_1_q[15:14]), .data(ram_3_data), .sel(1'b1), .ld(1'b1));  // open: clk, clr
  BitSelector #(.width(4)) bitselector_1 (.in(ram_1_data[8:5]), .out(Tiene_permiso), .sel(in_5));
  Hex_Digit_Display hex_digit_display_1 (.value(controlled_buffer_3_out[3:0]));  // open: dp
  Hex_Digit_Display hex_digit_display_2 (.value(controlled_buffer_3_out[7:4]));  // open: dp
  assign controlled_buffer_3_out = not_3_out ? ram_4_data : 8'bz;  // Controlled_Buffer controlled_buffer_3
  RAM #(.addrWidth(20)) ram_4 (
    .addr({ram_1_data[3:0], ram_3_data, multiplexer_1_out}), .data(ram_4_data), .sel(ram_1_data[4]),
    .clk(in_2), .ld(not_3_out));  // open: clr
  assign ram_4_data = Leer_Escribir ? register_3_q : 8'bz;  // Controlled_Buffer controlled_buffer_4
  Register register_3 (.D(controlled_buffer_1_out), .Q(register_3_q), .clk(in_3));  // open: en, clr
  not not_3 (not_3_out, Leer_Escribir);

  // Notes on the sheet:
  //   Dirección lógica de 22 bits
  //   Tabla de página de 64kb
  //   Tabla de segmento de 16kb
  //   Memoria principal de 1024KB
endmodule
