// Logisim project Final_NoTerminado.circ as structural Verilog: 1 circuit, main circuit main
module main (
  input  Ready_to_recieve_Slave_0,
  input  Ready_to_recieve_Slave_1,
  input  in_3,
  input  Ready_to_recieve_Slave_2,
  input  Ready_to_recieve_Slave_3,
  input  Ready_to_send,
  input  Ready_to_recieve_Slave_4,
  input  Ready_to_recieve_Slave_5,
  input  Ready_to_send_2,
  input  Ready_to_recieve_Slave_6,
  input  Ready_to_recieve_Slave_7,
  input  [10:0] Dir_Virtual,
  input  Escribir_0__Leer,
  input  in_14,
  output [7:0] Bus_Datos
);

  wire All_ready, and_1_out, and_3_out, and_4_out, and_5_out, and_6_out, and_8_out, Bus_ocupado, C, C1, C2,
       C3, C4, C5, C6, C7, C8, CargaD, CargaE, CargaM, CLK, counter_2_carry, decoder_2_out12,
       decoder_2_out13, decoder_2_out14, Error, ErrorE, ErrorM, Final_Ready_Master, Final_Ready_Slave,
       FinCiclo, FinT, Iniciar_Trasbase_q, not_1_out, not_2_out, not_3_out, not_6_out, not_7_out, not_8_out,
       not_9_out, not_10_out, not_11_out, not_12_out, not_13_out, or_3_out, or_4_out, or_5_out, or_6_out,
       or_7_out, or_8_out, ParidadE, ParidadGE, ParidadGM, ParidadM, Peticion_a_Maestro, Selector_Master,
       \Señal_mágica_de_haber_terminado , shift_register_1_out, shift_register_2_out, Slave_0, Slave_1,
       Slave_2, Slave_3, Slave_4, Slave_5, Slave_6, Slave_7, T0, T1, xor_1_out, xor_2_out, xor_3_out,
       xor_4_out, xor_5_out, xor_6_out, xor_7_out, xor_8_out, xor_9_out, xor_10_out, xor_11_out, xor_12_out,
       xor_13_out, xor_14_out, xor_15_out, xor_16_out, xor_17_out, xor_18_out, xor_19_out, xor_20_out,
       xor_21_out, xor_22_out, xor_23_out, xor_24_out, xor_27_out, xor_28_out;
  wire [1:0] ram_3_data;
  wire [2:0] controlled_buffer_1_out, final_ID, ID_destino_master_0;
  wire [3:0] counter_2_q, Posicion;
  wire [5:0] ram_4_data;
  wire [7:0] DatoPE, DatoPM, Datos_E, Datos_M, ram_1_data, ram_2_data, ram_13_data, ram_14_data;
  wire [9:0] counter_4_q, multiplexer_6_out;
  wire [10:0] multiplexer_5_out;

  Clock clock_1 (.out(CLK));
  Decoder #(.select(3), .disabled(0), .enable("false")) decoder_1 (
    .out0(Slave_0), .out1(Slave_1), .out2(Slave_2), .out3(Slave_3), .out4(Slave_4), .out5(Slave_5),
    .out6(Slave_6), .out7(Slave_7), .sel(controlled_buffer_1_out));
  assign controlled_buffer_1_out = All_ready ? final_ID : 3'bz;  // Controlled_Buffer controlled_buffer_1
  or or_1 (Error, ErrorE, ErrorM);
  Demultiplexer #(.enable("false")) demultiplexer_1 (.out0(T0), .out1(T1), .in(1'b1), .sel(Selector_Master));
  Multiplexer #(.enable("false")) multiplexer_1 (
    .in0(Ready_to_send), .in1(Ready_to_send_2), .out(Final_Ready_Master), .sel(Selector_Master));
  Multiplexer #(.width(3), .enable("false")) multiplexer_2 (
    .in0(ID_destino_master_0), .in1(ID_destino_master_0), .out(final_ID), .sel(Selector_Master));
  xor xor_1 (xor_1_out, DatoPM[0], DatoPM[1]);
  xor xor_2 (xor_2_out, xor_1_out, DatoPM[2]);
  xor xor_3 (xor_3_out, DatoPE[0], DatoPE[1]);
  xor xor_4 (xor_4_out, xor_3_out, DatoPE[2]);
  xor xor_5 (xor_5_out, Datos_M[0], Datos_M[1]);
  xor xor_6 (xor_6_out, Datos_E[0], Datos_E[1]);
  and and_1 (and_1_out, CLK, \Señal_mágica_de_haber_terminado );
  RAM #(.addrWidth(4)) ram_1 (.addr(Posicion), .data(ram_1_data), .sel(T0), .clk(CLK), .ld(CargaM));  // open: clr
  RAM #(.addrWidth(4)) ram_2 (.addr(Posicion), .data(ram_2_data), .sel(T1), .clk(CLK), .ld(CargaM));  // open: clr
  Multiplexer #(.select(3), .disabled(0), .enable("false")) multiplexer_3 (
    .in0(Ready_to_recieve_Slave_0), .in1(Ready_to_recieve_Slave_1), .in2(Ready_to_recieve_Slave_2),
    .in3(Ready_to_recieve_Slave_3), .in4(Ready_to_recieve_Slave_4), .in5(Ready_to_recieve_Slave_5),
    .in6(Ready_to_recieve_Slave_6), .in7(Ready_to_recieve_Slave_7), .out(Final_Ready_Slave), .sel(final_ID));
  or or_2 (C, C1, C2, C3, C4, C5, C6, C7, C8);
  xor xor_7 (xor_7_out, xor_2_out, DatoPM[3]);
  xor xor_8 (xor_8_out, xor_4_out, DatoPE[3]);
  xor xor_9 (xor_9_out, xor_5_out, Datos_M[2]);
  xor xor_10 (xor_10_out, xor_9_out, Datos_M[3]);
  xor xor_11 (xor_11_out, xor_6_out, Datos_E[2]);
  xor xor_12 (xor_12_out, xor_11_out, Datos_E[3]);
  and and_2 (All_ready, Final_Ready_Slave, Final_Ready_Master);
  Counter #(.width(1), .max('h1)) counter_1 (
    .D(1'b1), .Q(Selector_Master), .carry(Selector_Master), .clk(and_1_out));  // open: load, count, clr
  xor xor_13 (xor_13_out, xor_7_out, DatoPM[4]);
  xor xor_14 (xor_14_out, xor_13_out, DatoPM[5]);
  xor xor_15 (xor_15_out, xor_8_out, DatoPE[4]);
  xor xor_16 (xor_16_out, xor_15_out, DatoPE[5]);
  xor xor_17 (xor_17_out, xor_10_out, Datos_M[4]);
  xor xor_18 (xor_18_out, xor_17_out, Datos_M[5]);
  xor xor_19 (xor_19_out, xor_12_out, Datos_E[4]);
  xor xor_20 (xor_20_out, xor_19_out, Datos_E[5]);
  not not_1 (not_1_out, All_ready);
  not not_2 (not_2_out, CargaM);
  not not_3 (not_3_out, CargaM);
  xor xor_21 (xor_21_out, xor_14_out, DatoPM[6]);
  xor xor_22 (xor_22_out, xor_16_out, DatoPE[6]);
  xor xor_23 (xor_23_out, xor_18_out, Datos_M[6]);
  xor xor_24 (xor_24_out, xor_20_out, Datos_E[6]);
  Counter #(.width(4), .max('hf)) counter_2 (
    .Q(counter_2_q), .carry(counter_2_carry), .clk(CLK), .clr(or_3_out));  // open: load, D, count
  or or_3 (or_3_out, not_1_out, and_3_out);
  assign ram_1_data = not_2_out ? Datos_M : 8'bz;  // Controlled_Buffer controlled_buffer_2
  assign ram_2_data = not_3_out ? Datos_M : 8'bz;  // Controlled_Buffer controlled_buffer_3
  xor xor_25 (ParidadM, xor_21_out, DatoPM[7]);
  xor xor_26 (ParidadE, xor_22_out, DatoPE[7]);
  xor xor_27 (xor_27_out, xor_23_out, Datos_M[7]);
  xor xor_28 (xor_28_out, xor_24_out, Datos_E[7]);
  Decoder #(.select(4), .enable("false")) decoder_2 (
    .out1(CargaD), .out3(C1), .out4(C2), .out5(C3), .out6(C4), .out7(C5), .out8(C6), .out9(C7), .out10(C8),
    .out12(decoder_2_out12), .out13(decoder_2_out13), .out14(decoder_2_out14), .out15(FinCiclo),
    .sel(counter_2_q));  // open: out0, out2, out11
  and and_3 (and_3_out, decoder_2_out12, or_4_out);
  Multiplexer #(.width(8), .enable("false")) multiplexer_4 (
    .in0(ram_1_data), .in1(ram_2_data), .out(DatoPM), .sel(Selector_Master));
  xor xor_29 (ErrorE, xor_27_out, ParidadGE);
  xor xor_30 (ErrorM, xor_28_out, ParidadGM);
  or or_4 (or_4_out, Error, in_3);
  Shift_Register #(.length(9)) shift_register_1 (
    .in(shift_register_2_out), .clk(or_5_out), .out(shift_register_1_out), .load(CargaD), .d0(DatoPM[7]),
    .q0(Datos_M[7]), .d1(DatoPM[6]), .q1(Datos_M[6]), .d2(DatoPM[5]), .q2(Datos_M[5]), .d3(DatoPM[4]),
    .q3(Datos_M[4]), .d4(DatoPM[3]), .q4(Datos_M[3]), .d5(DatoPM[2]), .q5(Datos_M[2]), .d6(DatoPM[1]),
    .q6(Datos_M[1]), .d7(DatoPM[0]), .q7(Datos_M[0]), .d8(ParidadM), .q8(ParidadGE));  // open: shift, clr
  not not_4 (CargaE, decoder_2_out14);
  not not_5 (CargaM, decoder_2_out13);
  or or_5 (or_5_out, and_4_out, CargaD);
  and and_4 (and_4_out, C, CLK);
  Shift_Register #(.length(9)) shift_register_2 (
    .in(shift_register_1_out), .clk(or_5_out), .out(shift_register_2_out), .load(CargaD), .d0(DatoPE[7]),
    .q0(Datos_E[7]), .d1(DatoPE[6]), .q1(Datos_E[6]), .d2(DatoPE[5]), .q2(Datos_E[5]), .d3(DatoPE[4]),
    .q3(Datos_E[4]), .d4(DatoPE[3]), .q4(Datos_E[3]), .d5(DatoPE[2]), .q5(Datos_E[2]), .d6(DatoPE[1]),
    .q6(Datos_E[1]), .d7(DatoPE[0]), .q7(Datos_E[0]), .d8(ParidadE), .q8(ParidadGM));  // open: shift, clr
  Counter #(.width(5), .max('h10)) counter_3 (
    .Q({\Señal_mágica_de_haber_terminado , Posicion}), .clk(counter_2_carry),
    .clr(\Señal_mágica_de_haber_terminado ));  // open: load, D, count, carry
  RAM #(.addrWidth(2), .dataWidth(2)) ram_3 (
    .addr(Dir_Virtual[5:4]), .data(ram_3_data), .sel(1'b1), .ld(1'b1));  // open: clk, clr
  RAM #(.addrWidth(5), .dataWidth(6)) ram_4 (
    .addr(Dir_Virtual[10:6]), .data({ram_4_data[5:4], ID_destino_master_0, ram_4_data[0]}), .sel(1'b1),
    .ld(1'b1));  // open: clk, clr
  and and_5 (and_5_out, ~Bus_ocupado, in_14);  // AND_Gate
  Register #(.width(1)) Iniciar_Trasbase (.D(and_5_out), .Q(Iniciar_Trasbase_q), .clk(CLK), .clr(FinT));  // open: en
  RAM #(.addrWidth(4)) ram_5 (.addr(Posicion), .data(DatoPE), .sel(Slave_0), .clk(CLK), .ld(CargaE));  // open: clr
  RAM #(.addrWidth(4)) ram_6 (.addr(Posicion), .data(DatoPE), .sel(Slave_1), .clk(CLK), .ld(CargaE));  // open: clr
  RAM #(.addrWidth(4)) ram_7 (.addr(Posicion), .data(DatoPE), .sel(Slave_2), .clk(CLK), .ld(CargaE));  // open: clr
  RAM #(.addrWidth(4)) ram_8 (.addr(Posicion), .data(DatoPE), .sel(Slave_3), .clk(CLK), .ld(CargaE));  // open: clr
  RAM #(.addrWidth(4)) ram_9 (.addr(Posicion), .data(DatoPE), .sel(Slave_4), .clk(CLK), .ld(CargaE));  // open: clr
  RAM #(.addrWidth(4)) ram_10 (.addr(Posicion), .data(DatoPE), .sel(Slave_5), .clk(CLK), .ld(CargaE));  // open: clr
  RAM #(.addrWidth(4)) ram_11 (.addr(Posicion), .data(DatoPE), .sel(Slave_6), .clk(CLK), .ld(CargaE));  // open: clr
  RAM #(.addrWidth(4)) ram_12 (.addr(Posicion), .data(DatoPE), .sel(Slave_7), .clk(CLK), .ld(CargaE));  // open: clr
  Counter #(.width(10), .max('h3ff), .ongoal("stay")) counter_4 (
    .count(Iniciar_Trasbase_q), .Q(counter_4_q), .carry(FinT), .clk(CLK), .clr(FinT));  // open: load, D
  not not_6 (not_6_out, CargaE);
  not not_7 (not_7_out, CargaE);
  not not_8 (not_8_out, CargaE);
  not not_9 (not_9_out, CargaE);
  not not_10 (not_10_out, CargaE);
  not not_11 (not_11_out, CargaE);
  not not_12 (not_12_out, CargaE);
  not not_13 (not_13_out, CargaE);
  Multiplexer #(.width(11), .disabled(0), .enable("false")) multiplexer_5 (
    .in0({ram_4_data[4], ID_destino_master_0, ram_4_data[0], ram_3_data, Dir_Virtual[3:0]}),
    .in1({1'b1, counter_4_q}), .out(multiplexer_5_out), .sel(Iniciar_Trasbase_q));
  Multiplexer #(.width(10), .disabled(0), .enable("false")) multiplexer_6 (
    .in0({ID_destino_master_0, ram_4_data[0], ram_3_data, Dir_Virtual[3:0]}), .in1(counter_4_q),
    .out(multiplexer_6_out), .sel(Iniciar_Trasbase_q));
  or or_6 (or_6_out, Iniciar_Trasbase_q, FinCiclo);
  assign DatoPE = not_6_out ? Datos_E : 8'bz;  // Controlled_Buffer controlled_buffer_4
  assign DatoPE = not_7_out ? Datos_E : 8'bz;  // Controlled_Buffer controlled_buffer_5
  assign DatoPE = not_8_out ? Datos_E : 8'bz;  // Controlled_Buffer controlled_buffer_6
  assign DatoPE = not_9_out ? Datos_E : 8'bz;  // Controlled_Buffer controlled_buffer_7
  assign DatoPE = not_10_out ? Datos_E : 8'bz;  // Controlled_Buffer controlled_buffer_8
  assign DatoPE = not_11_out ? Datos_E : 8'bz;  // Controlled_Buffer controlled_buffer_9
  assign DatoPE = not_12_out ? Datos_E : 8'bz;  // Controlled_Buffer controlled_buffer_10
  assign DatoPE = not_13_out ? Datos_E : 8'bz;  // Controlled_Buffer controlled_buffer_11
  or or_7 (or_7_out, Peticion_a_Maestro, ram_4_data[5]);
  RAM #(.addrWidth(11)) ram_13 (
    .addr(multiplexer_5_out), .data(ram_13_data), .sel(or_7_out), .clk(CLK), .ld(Escribir_0__Leer));  // open: clr
  and and_6 (and_6_out, Escribir_0__Leer, ram_4_data[5]);
  and and_7 (Peticion_a_Maestro, ~ram_4_data[5], ~Escribir_0__Leer);  // AND_Gate
  RAM #(.addrWidth(10)) ram_14 (
    .addr(multiplexer_6_out), .data(ram_14_data), .sel(or_6_out), .clk(CLK), .ld(Iniciar_Trasbase_q));  // open: clr
  assign Bus_Datos = and_6_out ? ram_13_data : 8'bz;  // Controlled_Buffer controlled_buffer_12
  assign ram_13_data = or_8_out ? Bus_Datos : 8'bz;  // Controlled_Buffer controlled_buffer_13
  or or_8 (or_8_out, and_8_out, Peticion_a_Maestro);
  and and_8 (and_8_out, ~Escribir_0__Leer, ram_4_data[5]);  // AND_Gate
  assign Bus_Datos = Iniciar_Trasbase_q ? ram_14_data : 8'bz;  // Controlled_Buffer controlled_buffer_14
  assign ram_14_data = FinCiclo ? Datos_M : 8'bz;  // Controlled_Buffer controlled_buffer_15
  or or_9 (Bus_ocupado, and_6_out, and_8_out);

  // Other names for the same wires on the sheet: ID_destino_master_1[2:0] = ID_destino_master_0;
  //   NDisp[2:0] = ID_destino_master_0; Dato_Sistema[7:0] = Bus_Datos; Petición_Trasbase = in_14;
  //   Ready_Slave_0 = Ready_to_recieve_Slave_0; Ready_Slave_1 = Ready_to_recieve_Slave_1;
  //   Ready_Slave_2 = Ready_to_recieve_Slave_2; Ready_Slave_3 = Ready_to_recieve_Slave_3;
  //   Ready_Slave_4 = Ready_to_recieve_Slave_4; Ready_Slave_5 = Ready_to_recieve_Slave_5;
  //   Ready_Slave_6 = Ready_to_recieve_Slave_6; Ready_Slave_7 = Ready_to_recieve_Slave_7;
  //   Ready_to_send_master_0 = Ready_to_send; Ready_to_send_master_1 = Ready_to_send_2

  // Notes on the sheet:
  //   SELECTOR DEL ID ELEGIDA POR EL MASTER
  //   SELECTOR DE READY PARA SLAVE ELEGIDO POR EL MASTER
  //   SELECTOR DEL ESCLAVO SOLO CUANDO TODOS READY
  //   CICLO DE PASO DE INFORMACION
  //   GENERADORES DE PARIDAD
  //   COMPROBADOR DE PARIDAD
  //   LANZO EL CONTADOR 8-0 SI ESTA READY EL MASTER CON TOKEN
  //   offset
  //   DMA
  //   Bit que indica si está en memoria
  //   Memoria Física (32 paginas)
  //   Buffer del bus (16 paginas )
endmodule
