// Logisim project Handshake.circ as structural Verilog: 1 circuit, main circuit main
module main (
  input  Ready_to_recieve_Slave_0,
  input  Ready_to_recieve_Slave_1,
  input  Ready_to_recieve_Slave_2,
  input  in_4,
  input  Ready_to_recieve_Slave_3,
  input  [2:0] ID_Destino,
  input  Ready_to_send,
  input  Ready_to_recieve_Slave_4,
  input  Ready_to_recieve_Slave_5,
  input  [2:0] ID_Destino_2,
  input  Ready_to_send_2,
  input  Ready_to_recieve_Slave_6,
  input  Ready_to_recieve_Slave_7
);

  wire All_ready, and_1_out, CLK, Final_Ready_Master, Final_Ready_Slave, not_1_out, Selector_Master, Slave_0,
       Slave_1, Slave_2, Slave_3, Slave_4, Slave_5, Slave_6, Slave_7, T0, T1;
  wire [2:0] controlled_buffer_1_out, counter_2_q, final_ID;
  wire [7:0] Data_A, Data_B, ram_3_data;

  Clock clock_1 (.out(CLK));
  Decoder #(.select(3), .disabled(0), .enable("false")) decoder_1 (
    .out0(Slave_0), .out1(Slave_1), .out2(Slave_2), .out3(Slave_3), .out4(Slave_4), .out5(Slave_5),
    .out6(Slave_6), .out7(Slave_7), .sel(controlled_buffer_1_out));
  assign controlled_buffer_1_out = All_ready ? final_ID : 3'bz;  // Controlled_Buffer controlled_buffer_1
  Demultiplexer #(.enable("false")) demultiplexer_1 (.out0(T0), .out1(T1), .in(1'b1), .sel(Selector_Master));
  Multiplexer #(.enable("false")) multiplexer_1 (
    .in0(Ready_to_send), .in1(Ready_to_send_2), .out(Final_Ready_Master), .sel(Selector_Master));
  Multiplexer #(.width(3), .enable("false")) multiplexer_2 (
    .in0(ID_Destino), .in1(ID_Destino_2), .out(final_ID), .sel(Selector_Master));
  and and_1 (and_1_out, CLK, in_4);
  RAM #(.addrWidth(4)) ram_1 (.data(Data_A), .sel(T0), .clk(CLK));  // open: addr, ld, clr
  RAM #(.addrWidth(4)) ram_2 (.data(Data_B), .sel(T1), .clk(CLK));  // open: addr, ld, clr
  Multiplexer #(.select(3), .disabled(0), .enable("false")) multiplexer_3 (
    .in0(Ready_to_recieve_Slave_7), .in1(Ready_to_recieve_Slave_7), .in2(Ready_to_recieve_Slave_7),
    .in3(Ready_to_recieve_Slave_7), .in4(Ready_to_recieve_Slave_7), .in5(Ready_to_recieve_Slave_7),
    .in6(Ready_to_recieve_Slave_7), .in7(Ready_to_recieve_Slave_7), .out(Final_Ready_Slave), .sel(final_ID));
  and and_2 (All_ready, Final_Ready_Slave, Final_Ready_Master);
  Counter #(.width(1), .max('h1)) counter_1 (
    .D(1'b1), .Q(Selector_Master), .carry(Selector_Master), .clk(and_1_out));  // open: load, count, clr
  not not_1 (not_1_out, All_ready);
  Counter #(.width(3), .max('h7)) counter_2 (
    .Q(counter_2_q), .clk(CLK), .clr(not_1_out));  // open: load, D, count, carry
  Register register_1 ();  // open: D, en, Q, clk, clr
  RAM #(.addrWidth(4)) ram_3 (.data(ram_3_data), .sel(Slave_0), .clk(CLK));  // open: addr, ld, clr
  RAM #(.addrWidth(4)) ram_4 (.data(ram_3_data), .sel(Slave_1), .clk(CLK));  // open: addr, ld, clr
  RAM #(.addrWidth(4)) ram_5 (.data(ram_3_data), .sel(Slave_2), .clk(CLK));  // open: addr, ld, clr
  RAM #(.addrWidth(4)) ram_6 (.data(ram_3_data), .sel(Slave_3), .clk(CLK));  // open: addr, ld, clr
  RAM #(.addrWidth(4)) ram_7 (.data(ram_3_data), .sel(Slave_4), .clk(CLK));  // open: addr, ld, clr
  RAM #(.addrWidth(4)) ram_8 (.data(ram_3_data), .sel(Slave_5), .clk(CLK));  // open: addr, ld, clr
  RAM #(.addrWidth(4)) ram_9 (.data(ram_3_data), .sel(Slave_6), .clk(CLK));  // open: addr, ld, clr
  RAM #(.addrWidth(4)) ram_10 (.data(ram_3_data), .sel(Slave_7), .clk(CLK));  // open: addr, ld, clr
  Register register_2 ();  // open: D, en, Q, clk, clr

  // Other names for the same wires on the sheet: ID_destino_master_0[2:0] = ID_Destino;
  //   ID_destino_master_1[2:0] = ID_Destino_2; Ready_Slave_0 = Ready_to_recieve_Slave_0;
  //   Ready_Slave_1 = Ready_to_recieve_Slave_1; Ready_Slave_2 = Ready_to_recieve_Slave_2;
  //   Ready_Slave_3 = Ready_to_recieve_Slave_3; Ready_Slave_4 = Ready_to_recieve_Slave_4;
  //   Ready_Slave_5 = Ready_to_recieve_Slave_5; Ready_Slave_6 = Ready_to_recieve_Slave_6;
  //   Ready_Slave_7 = Ready_to_recieve_Slave_7; Ready_to_send_master_0 = Ready_to_send;
  //   Ready_to_send_master_1 = Ready_to_send_2; Señal_mágica_de_haber_terminado = in_4

  // Notes on the sheet:
  //   SELECTOR DEL ID ELEGIDA POR EL MASTER
  //   SELECTOR DE READY PARA SLAVE ELEGIDO POR EL MASTER
  //   SELECTOR DEL ESCLAVO SOLO CUANDO TODOS READY
  //   LANZO EL CONTADOR 8-0 SI ESTA READY EL MASTER CON TOKEN
endmodule
