// Logisim project Handshake_2.0.circ as structural Verilog: 1 circuit, main circuit main
module main (
  input  Ready_to_recieve_Slave_0,
  input  Ready_to_recieve_Slave_1,
  input  Ready_to_recieve_Slave_2,
  input  in_4,
  input  Ready_to_recieve_Slave_3,
  input  [2:0] ID_Destino,
  input  Ready_to_send,
  input  Ready_to_recieve_Slave_4,
  input  Ready_to_recieve_Slave_5,
  input  [2:0] ID_Destino_2,
  input  Ready_to_send_2,
  input  Ready_to_recieve_Slave_6,
  input  Ready_to_recieve_Slave_7
);

  wire All_ready, and_1_out, and_3_out, C, C1, C2, C3, C4, C5, C6, C7, CargaD, CargaE, CargaM, CLK,
       decoder_2_out10, decoder_2_out11, Final_Ready_Master, Final_Ready_Slave, not_1_out, not_2_out,
       not_3_out, not_6_out, not_7_out, not_8_out, not_9_out, not_10_out, not_11_out, not_12_out, not_13_out,
       or_2_out, RESET, Selector_Master, shift_register_1_out, shift_register_2_out, Slave_0, Slave_1,
       Slave_2, Slave_3, Slave_4, Slave_5, Slave_6, Slave_7, T0, T1;
  wire [2:0] controlled_buffer_1_out, final_ID;
  wire [3:0] counter_2_q, register_1_q, register_2_q, register_3_q, register_4_q, register_5_q, register_6_q,
       register_7_q, register_8_q, register_9_q, register_10_q;
  wire [7:0] Datos_E, Datos_M, multiplexer_4_out, ram_1_data, ram_2_data, ram_3_data;

  Clock clock_1 (.out(CLK));
  Register #(.width(4)) register_1 (.Q(register_1_q));  // open: D, en, clk, clr
  Register #(.width(4)) register_2 (.Q(register_2_q));  // open: D, en, clk, clr
  Decoder #(.select(3), .disabled(0), .enable("false")) decoder_1 (
    .out0(Slave_0), .out1(Slave_1), .out2(Slave_2), .out3(Slave_3), .out4(Slave_4), .out5(Slave_5),
    .out6(Slave_6), .out7(Slave_7), .sel(controlled_buffer_1_out));
  assign controlled_buffer_1_out = All_ready ? final_ID : 3'bz;  // Controlled_Buffer controlled_buffer_1
  Demultiplexer #(.enable("false")) demultiplexer_1 (.out0(T0), .out1(T1), .in(1'b1), .sel(Selector_Master));
  Multiplexer #(.enable("false")) multiplexer_1 (
    .in0(Ready_to_send), .in1(Ready_to_send_2), .out(Final_Ready_Master), .sel(Selector_Master));
  Multiplexer #(.width(3), .enable("false")) multiplexer_2 (
    .in0(ID_Destino), .in1(ID_Destino_2), .out(final_ID), .sel(Selector_Master));
  and and_1 (and_1_out, CLK, in_4);
  RAM #(.addrWidth(4)) ram_1 (.addr(register_1_q), .data(ram_1_data), .sel(T0), .clk(CLK), .ld(CargaM));  // open: clr
  RAM #(.addrWidth(4)) ram_2 (.addr(register_2_q), .data(ram_2_data), .sel(T1), .clk(CLK), .ld(CargaM));  // open: clr
  Multiplexer #(.select(3), .disabled(0), .enable("false")) multiplexer_3 (
    .in0(Ready_to_recieve_Slave_0), .in1(Ready_to_recieve_Slave_1), .in2(Ready_to_recieve_Slave_2),
    .in3(Ready_to_recieve_Slave_3), .in4(Ready_to_recieve_Slave_4), .in5(Ready_to_recieve_Slave_5),
    .in6(Ready_to_recieve_Slave_6), .in7(Ready_to_recieve_Slave_7), .out(Final_Ready_Slave), .sel(final_ID));
  or or_1 (C, C1, C2, C3, C4, C5, C6, C7);
  and and_2 (All_ready, Final_Ready_Slave, Final_Ready_Master);
  Counter #(.width(1), .max('h1)) counter_1 (
    .D(1'b1), .Q(Selector_Master), .carry(Selector_Master), .clk(and_1_out));  // open: load, count, clr
  not not_1 (not_1_out, All_ready);
  not not_2 (not_2_out, CargaM);
  not not_3 (not_3_out, CargaM);
  Counter #(.width(4), .max('hc)) counter_2 (
    .Q(counter_2_q), .clk(CLK), .clr(not_1_out));  // open: load, D, count, carry
  assign ram_1_data = not_2_out ? Datos_M : 8'bz;  // Controlled_Buffer controlled_buffer_2
  assign ram_2_data = not_3_out ? Datos_M : 8'bz;  // Controlled_Buffer controlled_buffer_3
  Decoder #(.select(4), .enable("false")) decoder_2 (
    .out1(CargaD), .out3(C1), .out4(C2), .out5(C3), .out6(C4), .out7(C5), .out8(C6), .out9(C7),
    .out10(decoder_2_out10), .out11(decoder_2_out11), .out13(RESET), .sel(counter_2_q));  // open: out0, out2, out12, out14, out15
  Multiplexer #(.width(8), .enable("false")) multiplexer_4 (
    .in0(ram_1_data), .in1(ram_2_data), .out(multiplexer_4_out), .sel(Selector_Master));
  Shift_Register shift_register_1 (
    .in(shift_register_2_out), .clk(or_2_out), .out(shift_register_1_out), .load(CargaD),
    .d0(multiplexer_4_out[7]), .q0(Datos_M[7]), .d1(multiplexer_4_out[6]), .q1(Datos_M[6]),
    .d2(multiplexer_4_out[5]), .q2(Datos_M[5]), .d3(multiplexer_4_out[4]), .q3(Datos_M[4]),
    .d4(multiplexer_4_out[3]), .q4(Datos_M[3]), .d5(multiplexer_4_out[2]), .q5(Datos_M[2]),
    .d6(multiplexer_4_out[1]), .q6(Datos_M[1]), .d7(multiplexer_4_out[0]), .q7(Datos_M[0]));  // open: shift, clr
  not not_4 (CargaE, decoder_2_out11);
  not not_5 (CargaM, decoder_2_out10);
  or or_2 (or_2_out, and_3_out, CargaD);
  and and_3 (and_3_out, C, CLK);
  Shift_Register shift_register_2 (
    .in(shift_register_1_out), .clk(or_2_out), .out(shift_register_2_out), .load(CargaD), .d0(ram_3_data[7]),
    .q0(Datos_E[7]), .d1(ram_3_data[6]), .q1(Datos_E[6]), .d2(ram_3_data[5]), .q2(Datos_E[5]),
    .d3(ram_3_data[4]), .q3(Datos_E[4]), .d4(ram_3_data[3]), .q4(Datos_E[3]), .d5(ram_3_data[2]),
    .q5(Datos_E[2]), .d6(ram_3_data[1]), .q6(Datos_E[1]), .d7(ram_3_data[0]), .q7(Datos_E[0]));  // open: shift, clr
  Register #(.width(4)) register_3 (.Q(register_3_q));  // open: D, en, clk, clr
  Register #(.width(4)) register_4 (.Q(register_4_q));  // open: D, en, clk, clr
  Register #(.width(4)) register_5 (.Q(register_5_q));  // open: D, en, clk, clr
  Register #(.width(4)) register_6 (.Q(register_6_q));  // open: D, en, clk, clr
  Register #(.width(4)) register_7 (.Q(register_7_q));  // open: D, en, clk, clr
  Register #(.width(4)) register_8 (.Q(register_8_q));  // open: D, en, clk, clr
  Register #(.width(4)) register_9 (.Q(register_9_q));  // open: D, en, clk, clr
  Register #(.width(4)) register_10 (.Q(register_10_q));  // open: D, en, clk, clr
  RAM #(.addrWidth(4)) ram_3 (
    .addr(register_3_q), .data(ram_3_data), .sel(Slave_0), .clk(CLK), .ld(CargaE));  // open: clr
  RAM #(.addrWidth(4)) ram_4 (
    .addr(register_4_q), .data(ram_3_data), .sel(Slave_1), .clk(CLK), .ld(CargaE));  // open: clr
  RAM #(.addrWidth(4)) ram_5 (
    .addr(register_5_q), .data(ram_3_data), .sel(Slave_2), .clk(CLK), .ld(CargaE));  // open: clr
  RAM #(.addrWidth(4)) ram_6 (
    .addr(register_6_q), .data(ram_3_data), .sel(Slave_3), .clk(CLK), .ld(CargaE));  // open: clr
  RAM #(.addrWidth(4)) ram_7 (
    .addr(register_7_q), .data(ram_3_data), .sel(Slave_4), .clk(CLK), .ld(CargaE));  // open: clr
  RAM #(.addrWidth(4)) ram_8 (
    .addr(register_8_q), .data(ram_3_data), .sel(Slave_5), .clk(CLK), .ld(CargaE));  // open: clr
  RAM #(.addrWidth(4)) ram_9 (
    .addr(register_9_q), .data(ram_3_data), .sel(Slave_6), .clk(CLK), .ld(CargaE));  // open: clr
  RAM #(.addrWidth(4)) ram_10 (
    .addr(register_10_q), .data(ram_3_data), .sel(Slave_7), .clk(CLK), .ld(CargaE));  // open: clr
  not not_6 (not_6_out, CargaE);
  not not_7 (not_7_out, CargaE);
  not not_8 (not_8_out, CargaE);
  not not_9 (not_9_out, CargaE);
  not not_10 (not_10_out, CargaE);
  not not_11 (not_11_out, CargaE);
  not not_12 (not_12_out, CargaE);
  not not_13 (not_13_out, CargaE);
  assign ram_3_data = not_6_out ? Datos_E : 8'bz;  // Controlled_Buffer controlled_buffer_4
  assign ram_3_data = not_7_out ? Datos_E : 8'bz;  // Controlled_Buffer controlled_buffer_5
  assign ram_3_data = not_8_out ? Datos_E : 8'bz;  // Controlled_Buffer controlled_buffer_6
  assign ram_3_data = not_9_out ? Datos_E : 8'bz;  // Controlled_Buffer controlled_buffer_7
  assign ram_3_data = not_10_out ? Datos_E : 8'bz;  // Controlled_Buffer controlled_buffer_8
  assign ram_3_data = not_11_out ? Datos_E : 8'bz;  // Controlled_Buffer controlled_buffer_9
  assign ram_3_data = not_12_out ? Datos_E : 8'bz;  // Controlled_Buffer controlled_buffer_10
  assign ram_3_data = not_13_out ? Datos_E : 8'bz;  // Controlled_Buffer controlled_buffer_11

  // Other names for the same wires on the sheet: ID_destino_master_0[2:0] = ID_Destino;
  //   ID_destino_master_1[2:0] = ID_Destino_2; Ready_Slave_0 = Ready_to_recieve_Slave_0;
  //   Ready_Slave_1 = Ready_to_recieve_Slave_1; Ready_Slave_2 = Ready_to_recieve_Slave_2;
  //   Ready_Slave_3 = Ready_to_recieve_Slave_3; Ready_Slave_4 = Ready_to_recieve_Slave_4;
  //   Ready_Slave_5 = Ready_to_recieve_Slave_5; Ready_Slave_6 = Ready_to_recieve_Slave_6;
  //   Ready_Slave_7 = Ready_to_recieve_Slave_7; Ready_to_send_master_0 = Ready_to_send;
  //   Ready_to_send_master_1 = Ready_to_send_2; Señal_mágica_de_haber_terminado = in_4

  // Notes on the sheet:
  //   SELECTOR DEL ID ELEGIDA POR EL MASTER
  //   SELECTOR DE READY PARA SLAVE ELEGIDO POR EL MASTER
  //   SELECTOR DEL ESCLAVO SOLO CUANDO TODOS READY
  //   CICLO DE PASO DE INFORMACION
  //   LANZO EL CONTADOR 8-0 SI ESTA READY EL MASTER CON TOKEN
endmodule
