// Logisim project Maestro-Esclavo.circ as structural Verilog: 1 circuit, main circuit main
module main (
  input  in_1
);

  wire and_1_out, CLK, counter_1_q, Selector_Master, T0, T1;
  wire [7:0] Data_A, Data_B, ram_3_data;

  Clock clock_1 (.out(CLK));
  Demultiplexer #(.enable("false")) demultiplexer_1 (.out0(T0), .out1(T1), .in(1'b1), .sel(Selector_Master));
  and and_1 (and_1_out, CLK, in_1);
  Counter #(.width(1), .max('h1)) counter_1 (
    .D(1'b1), .Q(counter_1_q), .carry(counter_1_q), .clk(and_1_out));  // open: load, count, clr
  RAM #(.addrWidth(4)) ram_1 (.data(Data_A), .sel(T0), .clk(CLK));  // open: addr, ld, clr
  RAM #(.addrWidth(4)) ram_2 (.data(Data_B), .sel(T1), .clk(CLK));  // open: addr, ld, clr
  Register #(.width(1)) register_1 (.D(counter_1_q), .Q(Selector_Master), .clk(CLK));  // open: en, clr
  Register register_2 ();  // open: D, en, Q, clk, clr
  RAM #(.addrWidth(4)) ram_3 (.data(ram_3_data), .clk(CLK));  // open: addr, sel, ld, clr
  RAM #(.addrWidth(4)) ram_4 (.data(ram_3_data), .clk(CLK));  // open: addr, sel, ld, clr
  RAM #(.addrWidth(4)) ram_5 (.data(ram_3_data), .clk(CLK));  // open: addr, sel, ld, clr
  RAM #(.addrWidth(4)) ram_6 (.data(ram_3_data), .clk(CLK));  // open: addr, sel, ld, clr
  RAM #(.addrWidth(4)) ram_7 (.data(ram_3_data), .clk(CLK));  // open: addr, sel, ld, clr
  RAM #(.addrWidth(4)) ram_8 (.data(ram_3_data), .clk(CLK));  // open: addr, sel, ld, clr
  RAM #(.addrWidth(4)) ram_9 (.data(ram_3_data), .clk(CLK));  // open: addr, sel, ld, clr
  RAM #(.addrWidth(4)) ram_10 (.data(ram_3_data), .clk(CLK));  // open: addr, sel, ld, clr
  Register register_3 ();  // open: D, en, Q, clk, clr

  // Other names for the same wires on the sheet: Señal_mágica_de_haber_terminado = in_1
endmodule
