// Logisim project Round-robin.circ as structural Verilog: 1 circuit, main circuit main
module main (
  input  in_1
);

  wire and_1_out, clock_1_out, \Salida_mágica_del_RR ;

  Clock clock_1 (.out(clock_1_out));
  and and_1 (and_1_out, clock_1_out, in_1);
  Counter #(.width(1), .max('h1)) counter_1 (
    .D(1'b1), .Q(\Salida_mágica_del_RR ), .carry(\Salida_mágica_del_RR ), .clk(and_1_out));  // open: load, count, clr

  // Other names for the same wires on the sheet: Señal_mágica_de_haber_terminado = in_1
endmodule
