// Logisim project Sistema-DMA.circ as structural Verilog: 1 circuit, main circuit main
module main (
  input  [10:0] Dir_Virtual,
  input  [7:0] in_2,
  input  in_3,
  input  in_4,
  input  in_5,
  input  Escribir_0__Leer,
  output [7:0] Bus_Datos
);

  wire and_1_out, and_2_out, and_3_out, and_5_out, CLK, Fin_Trasbase, Iniciar_Trasbase_q, not_1_out,
       or_1_out, or_2_out, or_3_out, Peticion_a_Maestro;
  wire [1:0] ram_1_data;
  wire [2:0] NDisp;
  wire [5:3] ram_2_data;
  wire [7:0] ram_3_data, ram_4_data;
  wire [9:0] counter_1_q, multiplexer_2_out;
  wire [10:0] multiplexer_1_out;

  Clock clock_1 (.out(CLK));
  not not_1 (not_1_out, in_4);
  RAM #(.addrWidth(2), .dataWidth(2)) ram_1 (
    .addr(Dir_Virtual[5:4]), .data(ram_1_data), .sel(1'b1), .ld(1'b1));  // open: clk, clr
  RAM #(.addrWidth(5), .dataWidth(6)) ram_2 (
    .addr(Dir_Virtual[10:6]), .data({ram_2_data, NDisp}), .sel(1'b1), .ld(1'b1));  // open: clk, clr
  and and_1 (and_1_out, ~in_5, in_4);  // AND_Gate
  Register #(.width(1)) Iniciar_Trasbase (
    .D(and_1_out), .Q(Iniciar_Trasbase_q), .clk(CLK), .clr(not_1_out));  // open: en
  Counter #(.width(10), .max('h3ff), .ongoal("stay")) counter_1 (
    .count(Iniciar_Trasbase_q), .Q(counter_1_q), .carry(Fin_Trasbase), .clk(CLK), .clr(not_1_out));  // open: load, D
  Multiplexer #(.width(11), .disabled(0), .enable("false")) multiplexer_1 (
    .in0({ram_2_data[4:3], NDisp, ram_1_data, Dir_Virtual[3:0]}), .in1({1'b1, counter_1_q}),
    .out(multiplexer_1_out), .sel(Iniciar_Trasbase_q));
  Multiplexer #(.width(10), .disabled(0), .enable("false")) multiplexer_2 (
    .in0({ram_2_data[3], NDisp, ram_1_data, Dir_Virtual[3:0]}), .in1(counter_1_q), .out(multiplexer_2_out),
    .sel(Iniciar_Trasbase_q));
  or or_1 (or_1_out, Iniciar_Trasbase_q, in_3);
  and and_2 (and_2_out, or_2_out, ~Iniciar_Trasbase_q);  // AND_Gate
  or or_2 (or_2_out, Escribir_0__Leer, Peticion_a_Maestro);
  RAM #(.addrWidth(11)) ram_3 (
    .addr(multiplexer_1_out), .data(ram_3_data), .clk(CLK), .ld(and_2_out));  // open: sel, clr
  and and_3 (and_3_out, or_2_out, ~Iniciar_Trasbase_q);  // AND_Gate
  and and_4 (Peticion_a_Maestro, ~ram_2_data[5], ~Escribir_0__Leer);  // AND_Gate
  RAM #(.addrWidth(10)) ram_4 (
    .addr(multiplexer_2_out), .data(ram_4_data), .sel(or_1_out), .clk(CLK), .ld(Iniciar_Trasbase_q));  // open: clr
  assign Bus_Datos = and_3_out ? ram_3_data : 8'bz;  // Controlled_Buffer controlled_buffer_1
  assign ram_3_data = or_3_out ? Bus_Datos : 8'bz;  // Controlled_Buffer controlled_buffer_2
  or or_3 (or_3_out, and_5_out, Iniciar_Trasbase_q);
  and and_5 (and_5_out, ~Escribir_0__Leer, ram_2_data[5]);  // AND_Gate
  assign Bus_Datos = Iniciar_Trasbase_q ? ram_4_data : 8'bz;  // Controlled_Buffer controlled_buffer_3
  assign ram_4_data = in_3 ? in_2 : 8'bz;  // Controlled_Buffer controlled_buffer_4

  // Other names for the same wires on the sheet: Bus_ocupado = in_5; Dato_Maestro[7:0] = in_2;
  //   Dato_Sistema[7:0] = Bus_Datos; Master_Accediendo = in_3; Petición_Trasbase = in_4

  // Notes on the sheet:
  //   offset
  //   1 página = 16 palabras(1B cada una)
  //   Bit que indica si está en memoria
endmodule
