// Logisim project Práctica de las diapositivas 1.1.circ as structural Verilog: 1 circuit, main circuit main
module main (
  input  in_1
);

  wire and_1_out, clock_1_out, not_1_out;
  wire [3:0] counter_1_q;

  Counter #(.width(4), .max('hf)) counter_1 (
    .Q(counter_1_q), .clk(and_1_out), .clr(in_1));  // open: load, D, count, carry
  // Probe on counter_1_q[0]
  // Probe on counter_1_q[1]
  // Probe on counter_1_q[2]
  // Probe on counter_1_q[3]
  Clock clock_1 (.out(clock_1_out));
  and and_1 (and_1_out, clock_1_out, not_1_out);
  Hex_Digit_Display hex_digit_display_1 (.value(counter_1_q));  // open: dp
  not not_1 (not_1_out, counter_1_q[3]);
endmodule
